// Logisim project rv32i_single_cycle.circ as structural Verilog: 6 circuits, main circuit cpu
module cpu (
  input  clock,
  input  reset,
  output [31:0] alu_operand_b,
  output [31:0] JalrTarget,
  output [31:0] alu_operand_a,
  output [31:0] result,
  output zero,
  output [31:0] tLuiOp3,
  output [31:0] instruction_op,
  output [31:0] pc_op
);

  wire and_1_out, comparator_1_eq, Control1_alu_src, Control1_branch, Control1_jal, Control1_jalr,
       Control1_lui, Control1_memtoreg, Control1_memwrite, Control1_reg_write, or_1_out;
  wire [1:0] Control1_operation;
  wire [2:0] InsructionFetch1_funct3;
  wire [4:0] InsructionFetch1_rd, InsructionFetch1_rs1, InsructionFetch1_rs2;
  wire [6:0] InsructionFetch1_funct7, InsructionFetch1_opcode;
  wire [11:0] InsructionFetch1_immediate;
  wire [31:0] adder_1_out, bit_extender_1_out, datamemory_1_read_data, multiplexer_1_out, multiplexer_2_out,
       RegFile1_read_data_2;

  instruction_fetch InsructionFetch1 (
    .Jalrtarget(JalrTarget), .Jalr(Control1_jalr), .clock(clock), .reset(reset), .PCSrc(or_1_out),
    .opcode(InsructionFetch1_opcode), .rd(InsructionFetch1_rd), .funct3(InsructionFetch1_funct3),
    .rs1(InsructionFetch1_rs1), .instruction(instruction_op), .rs2(InsructionFetch1_rs2),
    .funct7(InsructionFetch1_funct7), .immediate(InsructionFetch1_immediate), .pc(pc_op));  // open: t1Op, t2Op
  Adder #(.width(32)) adder_1 (.a(pc_op), .b(32'h4), .out(adder_1_out));  // open: cin, cout
  Multiplexer #(.width(32)) multiplexer_1 (
    .in0(multiplexer_2_out), .in1(adder_1_out), .out(multiplexer_1_out), .sel(Control1_jal));
  or or_1 (or_1_out, and_1_out, Control1_jal);
  Multiplexer #(.width(32)) multiplexer_2 (
    .in0(tLuiOp3), .in1({instruction_op[31:12], {12{1'b0}}}), .out(multiplexer_2_out), .sel(Control1_lui));
  Control Control1 (
    .opcode(InsructionFetch1_opcode), .funct3(InsructionFetch1_funct3), .funct7(InsructionFetch1_funct7),
    .reg_write(Control1_reg_write), .Operation(Control1_operation), .alu_src(Control1_alu_src),
    .MemWrite(Control1_memwrite), .MemToReg(Control1_memtoreg), .branch(Control1_branch), .LUI(Control1_lui),
    .JAL(Control1_jal), .JALR(Control1_jalr));
  assign bit_extender_1_out = {{20{InsructionFetch1_immediate[11]}}, InsructionFetch1_immediate};  // Bit_Extender bit_extender_1
  RegisterFile RegFile1 (
    .rs2(InsructionFetch1_rs2), .rs1(InsructionFetch1_rs1), .reset(reset), .write_data(multiplexer_1_out),
    .clock(clock), .reg_write(Control1_reg_write), .rd(InsructionFetch1_rd),
    .read_data_2(RegFile1_read_data_2), .read_data_1(alu_operand_a));
  Multiplexer #(.width(32)) multiplexer_3 (
    .in0(RegFile1_read_data_2), .in1(bit_extender_1_out), .out(alu_operand_b), .sel(Control1_alu_src));
  Comparator #(.width(32)) comparator_1 (
    .a(RegFile1_read_data_2), .b(alu_operand_a), .eq(comparator_1_eq));  // open: gt, lt
  ALU alu_1 (.A(alu_operand_a), .B(alu_operand_b), .Operation(Control1_operation), .result(result), .zero(zero));
  and and_1 (and_1_out, comparator_1_eq, Control1_branch);
  Multiplexer #(.width(32)) multiplexer_4 (
    .in0(result), .in1(datamemory_1_read_data), .out(tLuiOp3), .sel(Control1_memtoreg));
  assign JalrTarget = 32'hfffffffe & result;  // AND_Gate and_2, 32 bits wide
  DataMemory datamemory_1 (
    .address(result[9:2]), .MemWrite(Control1_memwrite), .clock(clock), .write_data(RegFile1_read_data_2),
    .read_data(datamemory_1_read_data));
endmodule

module instruction_fetch (
  input  [31:0] Jalrtarget,
  input  Jalr,
  input  clock,
  input  reset,
  input  PCSrc,
  output [6:0] opcode,
  output [4:0] rd,
  output [2:0] funct3,
  output [4:0] rs1,
  output [31:0] instruction,
  output [4:0] rs2,
  output [6:0] funct7,
  output [11:0] immediate,
  output [31:0] t1Op,
  output [31:0] pc,
  output [31:0] t2Op
);

  wire comparator_1_eq, comparator_2_eq;
  wire [31:0] adder_1_out, adder_2_out, multiplexer_1_out, multiplexer_2_out, multiplexer_3_out;

  Register #(.width(32)) register_1 (.D(multiplexer_1_out), .en(1'b1), .clk(clock), .Q(pc), .clr(reset));
  Multiplexer #(.width(32)) multiplexer_1 (
    .in0(multiplexer_2_out), .in1(Jalrtarget), .out(multiplexer_1_out), .sel(Jalr));
  Adder #(.width(32)) adder_1 (.a(pc), .b(32'h4), .out(adder_1_out));  // open: cin, cout
  Adder #(.width(32)) adder_2 (.a(pc), .b(multiplexer_3_out), .out(adder_2_out));  // open: cin, cout
  RAM #(.asyncread("true"), .dataWidth(32)) RAM1 (
    .addr(pc[9:2]), .we(1'b0), .oe(1'b1), .clk(clock),
    .dout({funct7, instruction[24:15], funct3, instruction[11:0]}));  // open: din
  Multiplexer #(.width(32)) multiplexer_2 (.in0(adder_1_out), .in1(adder_2_out), .out(multiplexer_2_out), .sel(PCSrc));
  Multiplexer #(.width(32)) multiplexer_3 (.in0(t1Op), .in1(t2Op), .out(multiplexer_3_out), .sel(comparator_1_eq));
  Comparator #(.width(7)) comparator_1 (.a(instruction[6:0]), .b(7'b1101111), .eq(comparator_1_eq));  // open: gt, lt
  Comparator #(.mode("unsigned"), .width(7)) comparator_2 (
    .a(7'b0100011), .b(instruction[6:0]), .eq(comparator_2_eq));  // open: gt, lt
  Multiplexer #(.width(12)) multiplexer_4 (
    .in0({funct7, instruction[24:20]}), .in1({funct7, instruction[11:7]}), .out(immediate),
    .sel(comparator_2_eq));
  assign t1Op = {{19{funct7[6]}}, {funct7[6], instruction[7], funct7[5:0], instruction[11:8], 1'b0}};  // Bit_Extender bit_extender_1
  assign t2Op = {{11{funct7[6]}}, {funct7[6], instruction[19:15], funct3, instruction[20], funct7[5:0], instruction[24:21], 1'b0}};  // Bit_Extender bit_extender_2

  assign {instruction[31:25], instruction[14:12]} = {funct7, funct3};
  assign opcode = instruction[6:0];
  assign rd = instruction[11:7];
  assign rs1 = instruction[19:15];
  assign rs2 = instruction[24:20];
endmodule

module RegisterFile (
  input  [4:0] rs2,
  input  [4:0] rs1,
  input  reset,
  input  [31:0] write_data,
  input  clock,
  input  reg_write,
  input  [4:0] rd,
  output [31:0] read_data_2,
  output [31:0] read_data_1
);

  wire and_1_out, and_2_out, and_3_out, and_4_out, and_5_out, and_6_out, and_7_out, and_8_out, and_9_out,
       and_10_out, and_11_out, and_12_out, and_13_out, and_14_out, and_15_out, and_16_out, and_17_out,
       and_18_out, and_19_out, and_20_out, and_21_out, and_22_out, and_23_out, and_24_out, and_25_out,
       and_26_out, and_27_out, and_28_out, and_29_out, and_30_out, and_31_out, decoder_1_out0,
       decoder_1_out1, decoder_1_out2, decoder_1_out3, decoder_1_out4, decoder_1_out5, decoder_1_out6,
       decoder_1_out7, decoder_1_out8, decoder_1_out9, decoder_1_out10, decoder_1_out11, decoder_1_out12,
       decoder_1_out13, decoder_1_out14, decoder_1_out15, decoder_1_out16, decoder_1_out17, decoder_1_out18,
       decoder_1_out19, decoder_1_out20, decoder_1_out21, decoder_1_out22, decoder_1_out23, decoder_1_out24,
       decoder_1_out25, decoder_1_out26, decoder_1_out27, decoder_1_out28, decoder_1_out29, decoder_1_out30,
       decoder_1_out31;
  wire [31:0] register_1_q, register_2_q, register_3_q, register_4_q, register_5_q, register_6_q,
       register_7_q, register_8_q, register_9_q, register_10_q, register_11_q, register_12_q, register_13_q,
       register_14_q, register_15_q, register_16_q, register_17_q, register_18_q, register_19_q,
       register_20_q, register_21_q, register_22_q, register_23_q, register_24_q, register_25_q,
       register_26_q, register_27_q, register_28_q, register_29_q, register_30_q, register_31_q;

  Decoder #(.enable("false"), .select(5)) decoder_1 (
    .out0(decoder_1_out0), .out1(decoder_1_out1), .out2(decoder_1_out2), .out3(decoder_1_out3),
    .out4(decoder_1_out4), .out5(decoder_1_out5), .out6(decoder_1_out6), .out7(decoder_1_out7),
    .out8(decoder_1_out8), .out9(decoder_1_out9), .out10(decoder_1_out10), .out11(decoder_1_out11),
    .out12(decoder_1_out12), .out13(decoder_1_out13), .out14(decoder_1_out14), .out15(decoder_1_out15),
    .out16(decoder_1_out16), .out17(decoder_1_out17), .out18(decoder_1_out18), .out19(decoder_1_out19),
    .out20(decoder_1_out20), .out21(decoder_1_out21), .out22(decoder_1_out22), .out23(decoder_1_out23),
    .out24(decoder_1_out24), .out25(decoder_1_out25), .out26(decoder_1_out26), .out27(decoder_1_out27),
    .out28(decoder_1_out28), .out29(decoder_1_out29), .out30(decoder_1_out30), .out31(decoder_1_out31),
    .sel(rd));
  and and_1 (and_1_out, reg_write, decoder_1_out8);
  and and_2 (and_2_out, reg_write, decoder_1_out16);
  and and_3 (and_3_out, reg_write, decoder_1_out24);
  Register #(.width(32)) register_1 (.D(write_data), .en(and_1_out), .clk(clock), .Q(register_1_q), .clr(reset));
  Register #(.width(32)) register_2 (.D(write_data), .en(and_2_out), .clk(clock), .Q(register_2_q), .clr(reset));
  Register #(.width(32)) register_3 (.D(write_data), .en(and_3_out), .clk(clock), .Q(register_3_q), .clr(reset));
  and and_4 (and_4_out, reg_write, decoder_1_out1);
  and and_5 (and_5_out, reg_write, decoder_1_out9);
  and and_6 (and_6_out, reg_write, decoder_1_out17);
  and and_7 (and_7_out, reg_write, decoder_1_out25);
  Register #(.width(32)) register_4 (.D(write_data), .en(and_4_out), .clk(clock), .Q(register_4_q), .clr(reset));
  Register #(.width(32)) register_5 (.D(write_data), .en(and_5_out), .clk(clock), .Q(register_5_q), .clr(reset));
  Register #(.width(32)) register_6 (.D(write_data), .en(and_6_out), .clk(clock), .Q(register_6_q), .clr(reset));
  Register #(.width(32)) register_7 (.D(write_data), .en(and_7_out), .clk(clock), .Q(register_7_q), .clr(reset));
  and and_8 (and_8_out, reg_write, decoder_1_out2);
  and and_9 (and_9_out, reg_write, decoder_1_out10);
  and and_10 (and_10_out, reg_write, decoder_1_out18);
  and and_11 (and_11_out, reg_write, decoder_1_out26);
  Register #(.width(32)) register_8 (.D(write_data), .en(and_8_out), .clk(clock), .Q(register_8_q), .clr(reset));
  Register #(.width(32)) register_9 (.D(write_data), .en(and_9_out), .clk(clock), .Q(register_9_q), .clr(reset));
  Register #(.width(32)) register_10 (.D(write_data), .en(and_10_out), .clk(clock), .Q(register_10_q), .clr(reset));
  Register #(.width(32)) register_11 (.D(write_data), .en(and_11_out), .clk(clock), .Q(register_11_q), .clr(reset));
  and and_12 (and_12_out, reg_write, decoder_1_out3);
  and and_13 (and_13_out, reg_write, decoder_1_out11);
  and and_14 (and_14_out, reg_write, decoder_1_out19);
  and and_15 (and_15_out, reg_write, decoder_1_out27);
  Register #(.width(32)) register_12 (.D(write_data), .en(and_12_out), .clk(clock), .Q(register_12_q), .clr(reset));
  Register #(.width(32)) register_13 (.D(write_data), .en(and_13_out), .clk(clock), .Q(register_13_q), .clr(reset));
  Register #(.width(32)) register_14 (.D(write_data), .en(and_14_out), .clk(clock), .Q(register_14_q), .clr(reset));
  Register #(.width(32)) register_15 (.D(write_data), .en(and_15_out), .clk(clock), .Q(register_15_q), .clr(reset));
  and and_16 (and_16_out, reg_write, decoder_1_out4);
  and and_17 (and_17_out, reg_write, decoder_1_out12);
  and and_18 (and_18_out, reg_write, decoder_1_out20);
  and and_19 (and_19_out, reg_write, decoder_1_out28);
  Register #(.width(32)) register_16 (.D(write_data), .en(and_16_out), .clk(clock), .Q(register_16_q), .clr(reset));
  Register #(.width(32)) register_17 (.D(write_data), .en(and_17_out), .clk(clock), .Q(register_17_q), .clr(reset));
  Register #(.width(32)) register_18 (.D(write_data), .en(and_18_out), .clk(clock), .Q(register_18_q), .clr(reset));
  Register #(.width(32)) register_19 (.D(write_data), .en(and_19_out), .clk(clock), .Q(register_19_q), .clr(reset));
  and and_20 (and_20_out, reg_write, decoder_1_out5);
  and and_21 (and_21_out, reg_write, decoder_1_out13);
  and and_22 (and_22_out, reg_write, decoder_1_out21);
  and and_23 (and_23_out, reg_write, decoder_1_out29);
  Register #(.width(32)) register_20 (.D(write_data), .en(and_20_out), .clk(clock), .Q(register_20_q), .clr(reset));
  Register #(.width(32)) register_21 (.D(write_data), .en(and_21_out), .clk(clock), .Q(register_21_q), .clr(reset));
  Register #(.width(32)) register_22 (.D(write_data), .en(and_22_out), .clk(clock), .Q(register_22_q), .clr(reset));
  Register #(.width(32)) register_23 (.D(write_data), .en(and_23_out), .clk(clock), .Q(register_23_q), .clr(reset));
  and and_24 (and_24_out, reg_write, decoder_1_out6);
  and and_25 (and_25_out, reg_write, decoder_1_out14);
  and and_26 (and_26_out, reg_write, decoder_1_out22);
  and and_27 (and_27_out, reg_write, decoder_1_out30);
  Register #(.width(32)) register_24 (.D(write_data), .en(and_24_out), .clk(clock), .Q(register_24_q), .clr(reset));
  Register #(.width(32)) register_25 (.D(write_data), .en(and_25_out), .clk(clock), .Q(register_25_q), .clr(reset));
  Register #(.width(32)) register_26 (.D(write_data), .en(and_26_out), .clk(clock), .Q(register_26_q), .clr(reset));
  Register #(.width(32)) register_27 (.D(write_data), .en(and_27_out), .clk(clock), .Q(register_27_q), .clr(reset));
  and and_28 (and_28_out, reg_write, decoder_1_out7);
  and and_29 (and_29_out, reg_write, decoder_1_out15);
  and and_30 (and_30_out, reg_write, decoder_1_out23);
  and and_31 (and_31_out, reg_write, decoder_1_out31);
  Register #(.width(32)) register_28 (.D(write_data), .en(and_28_out), .clk(clock), .Q(register_28_q), .clr(reset));
  Register #(.width(32)) register_29 (.D(write_data), .en(and_29_out), .clk(clock), .Q(register_29_q), .clr(reset));
  Register #(.width(32)) register_30 (.D(write_data), .en(and_30_out), .clk(clock), .Q(register_30_q), .clr(reset));
  Register #(.width(32)) register_31 (.D(write_data), .en(and_31_out), .clk(clock), .Q(register_31_q), .clr(reset));
  Multiplexer #(.select(5), .width(32)) multiplexer_1 (
    .in0({32{1'b0}}), .in1(register_4_q), .in2(register_8_q), .in3(register_12_q), .in4(register_16_q),
    .in5(register_20_q), .in6(register_24_q), .in7(register_28_q), .in8(register_1_q), .in9(register_5_q),
    .in10(register_9_q), .in11(register_13_q), .in12(register_17_q), .in13(register_21_q),
    .in14(register_25_q), .in15(register_29_q), .in16(register_2_q), .in17(register_6_q),
    .in18(register_10_q), .in19(register_14_q), .in20(register_18_q), .in21(register_22_q),
    .in22(register_26_q), .in23(register_30_q), .in24(register_3_q), .in25(register_7_q),
    .in26(register_11_q), .in27(register_15_q), .in28(register_19_q), .in29(register_23_q),
    .in30(register_27_q), .in31(register_31_q), .out(read_data_2), .sel(rs2));
  Multiplexer #(.select(5), .width(32)) multiplexer_2 (
    .in0({32{1'b0}}), .in1(register_4_q), .in2(register_8_q), .in3(register_12_q), .in4(register_16_q),
    .in5(register_20_q), .in6(register_24_q), .in7(register_28_q), .in8(register_1_q), .in9(register_5_q),
    .in10(register_9_q), .in11(register_13_q), .in12(register_17_q), .in13(register_21_q),
    .in14(register_25_q), .in15(register_29_q), .in16(register_2_q), .in17(register_6_q),
    .in18(register_10_q), .in19(register_14_q), .in20(register_18_q), .in21(register_22_q),
    .in22(register_26_q), .in23(register_30_q), .in24(register_3_q), .in25(register_7_q),
    .in26(register_11_q), .in27(register_15_q), .in28(register_19_q), .in29(register_23_q),
    .in30(register_27_q), .in31(register_31_q), .out(read_data_1), .sel(rs1));
endmodule

module ALU (
  input  [31:0] A,
  input  [31:0] B,
  input  [1:0] Operation,
  output [31:0] result,
  output zero
);

  wire [31:0] adder_1_out, and_1_out, or_1_out, subtractor_1_out;

  Adder #(.width(32)) adder_1 (.a(A), .b(B), .out(adder_1_out));  // open: cin, cout
  Subtractor #(.width(32)) subtractor_1 (.a(A), .b(B), .out(subtractor_1_out));  // open: bin, bout
  assign and_1_out = A & B;  // AND_Gate and_1, 32 bits wide
  assign or_1_out = A | B;  // OR_Gate or_1, 32 bits wide
  Multiplexer #(.select(2), .width(32)) multiplexer_1 (
    .in0(adder_1_out), .in1(subtractor_1_out), .in2(and_1_out), .in3(or_1_out), .out(result), .sel(Operation));
  Comparator #(.mode("unsigned"), .width(32)) comparator_1 (.a(result), .b({32{1'b0}}), .eq(zero));  // open: gt, lt
endmodule

module Control (
  input  [6:0] opcode,
  input  [2:0] funct3,
  input  [6:0] funct7,
  output reg_write,
  output [1:0] Operation,
  output alu_src,
  output MemWrite,
  output MemToReg,
  output branch,
  output LUI,
  output JAL,
  output JALR
);

  wire and_1_out, and_6_out, comparator_1_eq, comparator_2_eq, comparator_3_eq, comparator_4_eq,
       comparator_5_eq, comparator_6_eq, comparator_7_eq, comparator_8_eq, comparator_9_eq, comparator_10_eq,
       comparator_13_eq;

  Comparator #(.mode("unsigned"), .width(7)) comparator_1 (
    .a(7'b0110011), .b(opcode), .eq(comparator_1_eq));  // open: gt, lt
  Comparator #(.mode("unsigned"), .width(3)) comparator_2 (
    .a(3'b000), .b(funct3), .eq(comparator_2_eq));  // open: gt, lt
  Comparator #(.mode("unsigned"), .width(7)) comparator_3 (
    .a({7{1'b0}}), .b(funct7), .eq(comparator_3_eq));  // open: gt, lt
  Comparator #(.mode("unsigned"), .width(7)) comparator_4 (
    .a(7'b0010011), .b(opcode), .eq(comparator_4_eq));  // open: gt, lt
  Comparator #(.mode("unsigned"), .width(7)) comparator_5 (
    .a(7'b0000011), .b(opcode), .eq(comparator_5_eq));  // open: gt, lt
  Comparator #(.mode("unsigned"), .width(3)) comparator_6 (
    .a(3'b010), .b(funct3), .eq(comparator_6_eq));  // open: gt, lt
  Comparator #(.mode("unsigned"), .width(7)) comparator_7 (
    .a(7'b0100011), .b(opcode), .eq(comparator_7_eq));  // open: gt, lt
  Comparator #(.mode("unsigned"), .width(3)) comparator_8 (
    .a(3'b010), .b(funct3), .eq(comparator_8_eq));  // open: gt, lt
  Comparator #(.mode("unsigned"), .width(7)) comparator_9 (
    .a(7'b1100011), .b(opcode), .eq(comparator_9_eq));  // open: gt, lt
  Comparator #(.mode("unsigned"), .width(3)) comparator_10 (
    .a(3'b000), .b(funct3), .eq(comparator_10_eq));  // open: gt, lt
  Comparator #(.mode("unsigned"), .width(7)) comparator_11 (.a(7'b0110111), .b(opcode), .eq(LUI));  // open: gt, lt
  Comparator #(.mode("unsigned"), .width(7)) comparator_12 (.a(7'b1101111), .b(opcode), .eq(JAL));  // open: gt, lt
  Comparator #(.mode("unsigned"), .width(7)) comparator_13 (
    .a(7'b1100111), .b(opcode), .eq(comparator_13_eq));  // open: gt, lt
  and and_1 (and_1_out, comparator_2_eq, comparator_4_eq);
  and and_2 (MemToReg, comparator_5_eq, comparator_6_eq);
  and and_3 (MemWrite, comparator_7_eq, comparator_8_eq);
  and and_4 (branch, comparator_9_eq, comparator_10_eq);
  and and_5 (JALR, comparator_10_eq, comparator_13_eq);
  and and_6 (and_6_out, comparator_1_eq, comparator_2_eq, comparator_3_eq);
  or or_1 (reg_write, and_6_out, MemToReg, JAL, and_1_out, LUI, JALR);
  or or_2 (alu_src, and_1_out, MemToReg, MemWrite, JALR);

  assign Operation = 2'b00;
endmodule

module DataMemory (
  input  [7:0] address,
  input  MemWrite,
  input  clock,
  input  [31:0] write_data,
  output [31:0] read_data
);

  RAM #(.asyncread("true"), .dataWidth(32)) DataRam1 (
    .addr(address), .we(MemWrite), .oe(1'b1), .clk(clock), .din(write_data), .dout(read_data));
endmodule
