// Logisim project rv32i_pipelined.circ as structural Verilog
module IFetch (
  input  not_stall,
  input  clock,
  input  reset,
  input  [31:0] br_target,
  input  br_taken,
  output [31:0] instruction,
  output [31:0] pc
);

  wire [31:0] adder_1_out, multiplexer_1_out;

  Register #(.width(32)) register_1 (.D(multiplexer_1_out), .en(not_stall), .clk(clock), .Q(pc), .clr(reset));
  RAM #(.asyncread("true"), .dataWidth(32)) RAM1 (
    .addr(pc[9:2]), .we(1'b0), .oe(1'b1), .clk(clock), .dout(instruction));  // open: din
  Adder #(.width(32)) adder_1 (.a(32'h4), .b(pc), .out(adder_1_out));  // open: cin, cout
  Multiplexer #(.width(32)) multiplexer_1 (.in0(adder_1_out), .in1(br_target), .out(multiplexer_1_out), .sel(br_taken));
endmodule

module IDecode (
  input  [31:0] instruction,
  input  reset,
  input  clock,
  input  wb_reg_write,
  input  [31:0] pc,
  input  [31:0] wb_data,
  input  [4:0] wb_rd,
  output [6:0] opcode,
  output [1:0] result_src,
  output [4:0] rd,
  output alu_src,
  output [2:0] funct3,
  output mem_read,
  output [4:0] rs1,
  output mem_write,
  output [4:0] rs2,
  output reg_write,
  output [6:0] funct7,
  output branch,
  output alu_sub,
  output jump,
  output jalr,
  output [31:0] read_data_2,
  output [31:0] read_data_1,
  output [31:0] immediate,
  output [31:0] pc_op
);

  ImmediateGen ImmGen1 (.instruction(instruction), .immediate(immediate));
  ControlUnit controlunit_1 (
    .opcode(instruction[6:0]), .result_src(result_src), .alu_src(alu_src), .mem_read(mem_read),
    .reg_write(reg_write), .branch(branch), .mem_write(mem_write), .alu_sub(alu_sub), .jump(jump), .jalr(jalr));
  RegFile regfile_1 (
    .rs2(instruction[24:20]), .rs1(instruction[19:15]), .reset(reset), .write_data(wb_data), .clock(clock),
    .reg_write(wb_reg_write), .rd(wb_rd), .read_data_2(read_data_2), .read_data_1(read_data_1));

  assign funct3 = instruction[14:12];
  assign funct7 = instruction[31:25];
  assign opcode = instruction[6:0];
  assign pc_op = pc;
  assign rd = instruction[11:7];
  assign rs1 = instruction[19:15];
  assign rs2 = instruction[24:20];
endmodule

module cpu (
  input  clock,
  input  reset,
  output stall
);

  wire and_1_out, and_2_out, and_3_out, and_4_out, and_5_out, and_6_out, bubblecontrol_1_branch_op,
       bubblecontrol_1_jalr_op, bubblecontrol_1_jump_op, bubblecontrol_1_mem_read_op,
       bubblecontrol_1_mem_write_op, bubblecontrol_1_reg_write_op, ex_mem_1_mem_mem_read,
       ex_mem_1_mem_mem_write, ex_mem_1_mem_reg_write, execute_1_br_taken, id_ex_1_ex_alu_src,
       id_ex_1_ex_alu_sub, id_ex_1_ex_branch, id_ex_1_ex_jalr, id_ex_1_ex_jump, id_ex_1_ex_mem_read,
       id_ex_1_ex_mem_write, id_ex_1_ex_reg_write, idecode_1_alu_src, idecode_1_alu_sub, idecode_1_branch,
       idecode_1_jalr, idecode_1_jump, idecode_1_mem_read, idecode_1_mem_write, idecode_1_reg_write,
       mem_wb_1_wb_reg_write, not_1_out, not_2_out;
  wire [1:0] ex_mem_1_mem_result_src, id_ex_1_ex_result_src, idecode_1_result_src;
  wire [2:0] idecode_1_funct3;
  wire [4:0] ex_mem_1_mem_rd, ex_mem_1_mem_rs2, forwardingunit_1_ex_rs2_op, id_ex_1_ex_rd, id_ex_1_ex_rs1,
       id_ex_1_ex_rs2, idecode_1_rd, idecode_1_rs1, idecode_1_rs2, mem_wb_1_wb_rd;
  wire [6:0] idecode_1_funct7;
  wire [31:0] ex_mem_1_mem_alu_result, ex_mem_1_mem_immediate, ex_mem_1_mem_pc, ex_mem_1_mem_read_data_2,
       execute_1_br_target, execute_1_result, forwardingunit_1_read_data_1, forwardingunit_1_read_data_2,
       id_ex_1_ex_immediate, id_ex_1_ex_pc, id_ex_1_ex_read_data_1, id_ex_1_ex_read_data_2,
       idecode_1_immediate, idecode_1_pc_op, idecode_1_read_data_1, idecode_1_read_data_2,
       ifetch_1_instruction, ifetch_1_pc, mem_wb_1_wb_data, memory_1_read_data, multiplexer_1_out,
       multiplexer_2_out, register_1_q, register_2_q, storeforwardingunit_1_mem_store_data;

  IFetch ifetch_1 (
    .not_stall(not_2_out), .clock(clock), .reset(reset), .br_target(execute_1_br_target),
    .br_taken(execute_1_br_taken), .instruction(ifetch_1_instruction), .pc(ifetch_1_pc));
  Multiplexer #(.width(32)) multiplexer_1 (
    .in0(ifetch_1_instruction), .in1(32'h13), .out(multiplexer_1_out), .sel(execute_1_br_taken));
  Multiplexer #(.width(32)) multiplexer_2 (
    .in0(ifetch_1_pc), .in1({32{1'b0}}), .out(multiplexer_2_out), .sel(execute_1_br_taken));
  Register #(.width(32)) register_1 (.D(multiplexer_1_out), .en(not_2_out), .clk(clock), .Q(register_1_q), .clr(reset));
  Register #(.width(32)) register_2 (.D(multiplexer_2_out), .en(not_2_out), .clk(clock), .Q(register_2_q), .clr(reset));
  not not_1 (not_1_out, execute_1_br_taken);
  and and_1 (and_1_out, not_1_out, idecode_1_jump);
  IDecode idecode_1 (
    .instruction(register_1_q), .reset(reset), .clock(clock), .wb_reg_write(mem_wb_1_wb_reg_write),
    .pc(register_2_q), .wb_data(mem_wb_1_wb_data), .wb_rd(mem_wb_1_wb_rd), .result_src(idecode_1_result_src),
    .rd(idecode_1_rd), .alu_src(idecode_1_alu_src), .funct3(idecode_1_funct3), .mem_read(idecode_1_mem_read),
    .rs1(idecode_1_rs1), .mem_write(idecode_1_mem_write), .rs2(idecode_1_rs2),
    .reg_write(idecode_1_reg_write), .funct7(idecode_1_funct7), .branch(idecode_1_branch),
    .alu_sub(idecode_1_alu_sub), .jump(idecode_1_jump), .jalr(idecode_1_jalr),
    .read_data_2(idecode_1_read_data_2), .read_data_1(idecode_1_read_data_1),
    .immediate(idecode_1_immediate), .pc_op(idecode_1_pc_op));  // open: opcode
  and and_2 (and_2_out, idecode_1_branch, not_1_out);
  and and_3 (and_3_out, idecode_1_reg_write, not_1_out);
  and and_4 (and_4_out, idecode_1_mem_write, not_1_out);
  and and_5 (and_5_out, not_1_out, idecode_1_jalr);
  and and_6 (and_6_out, idecode_1_mem_read, not_1_out);
  HarzardDetectionUnit harzarddetectionunit_1 (
    .ex_rd(id_ex_1_ex_rd), .rs1(idecode_1_rs1), .rs2(idecode_1_rs2), .ex_mem_read(id_ex_1_ex_mem_read),
    .stall(stall));
  BubbleControl bubblecontrol_1 (
    .jalr(and_5_out), .reg_write(and_3_out), .mem_read(and_6_out), .mem_write(and_4_out), .branch(and_2_out),
    .jump(and_1_out), .not_stall(not_2_out), .jalr_op(bubblecontrol_1_jalr_op),
    .reg_write_op(bubblecontrol_1_reg_write_op), .mem_read_op(bubblecontrol_1_mem_read_op),
    .mem_write_op(bubblecontrol_1_mem_write_op), .branch_op(bubblecontrol_1_branch_op),
    .jump_op(bubblecontrol_1_jump_op));
  not not_2 (not_2_out, stall);
  ID_EX id_ex_1 (
    .pc(idecode_1_pc_op), .read_data_1(idecode_1_read_data_1), .read_data_2(idecode_1_read_data_2),
    .immediate(idecode_1_immediate), .rd(idecode_1_rd), .rs1(idecode_1_rs1), .rs2(idecode_1_rs2),
    .funct3(idecode_1_funct3), .funct7(idecode_1_funct7), .result_src(idecode_1_result_src),
    .alu_src(idecode_1_alu_src), .mem_read(bubblecontrol_1_mem_read_op),
    .mem_write(bubblecontrol_1_mem_write_op), .reg_write(bubblecontrol_1_reg_write_op),
    .branch(bubblecontrol_1_branch_op), .alu_sub(idecode_1_alu_sub), .jump(bubblecontrol_1_jump_op),
    .jalr(bubblecontrol_1_jalr_op), .reset(reset), .clock(clock), .enable(1'b1), .ex_pc(id_ex_1_ex_pc),
    .ex_read_data_1(id_ex_1_ex_read_data_1), .ex_read_data_2(id_ex_1_ex_read_data_2),
    .ex_immediate(id_ex_1_ex_immediate), .ex_rd(id_ex_1_ex_rd), .ex_rs1(id_ex_1_ex_rs1),
    .ex_rs2(id_ex_1_ex_rs2), .ex_result_src(id_ex_1_ex_result_src), .ex_alu_src(id_ex_1_ex_alu_src),
    .ex_mem_read(id_ex_1_ex_mem_read), .ex_mem_write(id_ex_1_ex_mem_write),
    .ex_reg_write(id_ex_1_ex_reg_write), .ex_branch(id_ex_1_ex_branch), .ex_alu_sub(id_ex_1_ex_alu_sub),
    .ex_jump(id_ex_1_ex_jump), .ex_jalr(id_ex_1_ex_jalr));  // open: ex_funct3, ex_funct7
  Execute execute_1 (
    .jump(id_ex_1_ex_jump), .jalr(id_ex_1_ex_jalr), .branch(id_ex_1_ex_branch), .pc(id_ex_1_ex_pc),
    .read_data_1(forwardingunit_1_read_data_1), .read_data_2(forwardingunit_1_read_data_2),
    .immediate(id_ex_1_ex_immediate), .alu_src(id_ex_1_ex_alu_src), .alu_sub(id_ex_1_ex_alu_sub),
    .br_target(execute_1_br_target), .br_taken(execute_1_br_taken), .result(execute_1_result));  // open: zero
  ForwardingUnit forwardingunit_1 (
    .ex_read_data_2(id_ex_1_ex_read_data_2), .wb_rd(mem_wb_1_wb_rd), .ex_read_data_1(id_ex_1_ex_read_data_1),
    .wb_reg_write(mem_wb_1_wb_reg_write), .wb_data(mem_wb_1_wb_data), .ex_rs1(id_ex_1_ex_rs1),
    .ex_rs2(id_ex_1_ex_rs2), .mem_rd(ex_mem_1_mem_rd), .mem_alu_result(ex_mem_1_mem_alu_result),
    .mem_reg_write(ex_mem_1_mem_reg_write), .mem_mem_read(ex_mem_1_mem_mem_read),
    .read_data_1(forwardingunit_1_read_data_1), .read_data_2(forwardingunit_1_read_data_2),
    .ex_rs2_op(forwardingunit_1_ex_rs2_op));
  EX_MEM ex_mem_1 (
    .pc(id_ex_1_ex_pc), .alu_result(execute_1_result), .read_data_2(forwardingunit_1_read_data_2),
    .rd(id_ex_1_ex_rd), .immediate(id_ex_1_ex_immediate), .result_src(id_ex_1_ex_result_src),
    .mem_read(id_ex_1_ex_mem_read), .mem_write(id_ex_1_ex_mem_write), .reg_write(id_ex_1_ex_reg_write),
    .jump(id_ex_1_ex_jump), .ex_rs2(forwardingunit_1_ex_rs2_op), .reset(reset), .clock(clock), .enable(1'b1),
    .mem_pc(ex_mem_1_mem_pc), .mem_alu_result(ex_mem_1_mem_alu_result),
    .mem_read_data_2(ex_mem_1_mem_read_data_2), .mem_rd(ex_mem_1_mem_rd),
    .mem_immediate(ex_mem_1_mem_immediate), .mem_result_src(ex_mem_1_mem_result_src),
    .mem_mem_read(ex_mem_1_mem_mem_read), .mem_mem_write(ex_mem_1_mem_mem_write),
    .mem_reg_write(ex_mem_1_mem_reg_write), .mem_rs2(ex_mem_1_mem_rs2));  // open: mem_jump
  StoreForwardingUnit storeforwardingunit_1 (
    .mem_read_data_2(ex_mem_1_mem_read_data_2), .wb_data(mem_wb_1_wb_data),
    .mem_mem_write(ex_mem_1_mem_mem_write), .wb_reg_write(mem_wb_1_wb_reg_write), .wb_rd(mem_wb_1_wb_rd),
    .mem_rs2(ex_mem_1_mem_rs2), .mem_store_data(storeforwardingunit_1_mem_store_data));
  Memory memory_1 (
    .address(ex_mem_1_mem_alu_result), .mem_write(ex_mem_1_mem_mem_write), .mem_read(ex_mem_1_mem_mem_read),
    .clock(clock), .write_data(storeforwardingunit_1_mem_store_data), .read_data(memory_1_read_data));
  MEM_WB mem_wb_1 (
    .pc(ex_mem_1_mem_pc), .alu_result(ex_mem_1_mem_alu_result), .read_data(memory_1_read_data),
    .rd(ex_mem_1_mem_rd), .immediate(ex_mem_1_mem_immediate), .result_src(ex_mem_1_mem_result_src),
    .reg_write(ex_mem_1_mem_reg_write), .reset(reset), .clock(clock), .enable(1'b1),
    .wb_data(mem_wb_1_wb_data), .wb_rd(mem_wb_1_wb_rd), .wb_reg_write(mem_wb_1_wb_reg_write));  // open: wb_pc, wb_alu_result, wb_read_data, wb_immediate, wb_result_src
endmodule

module RegFile (
  input  [4:0] rs2,
  input  [4:0] rs1,
  input  reset,
  input  [31:0] write_data,
  input  clock,
  input  reg_write,
  input  [4:0] rd,
  output [31:0] read_data_2,
  output [31:0] read_data_1
);

  wire and_1_out, and_2_out, and_3_out, and_4_out, and_5_out, and_6_out, and_7_out, and_8_out, and_9_out,
       and_10_out, and_11_out, and_12_out, and_13_out, and_14_out, and_15_out, and_16_out, and_17_out,
       and_18_out, and_19_out, and_20_out, and_21_out, and_22_out, and_23_out, and_24_out, and_25_out,
       and_26_out, and_27_out, and_28_out, and_29_out, and_30_out, and_31_out, decoder_1_out0,
       decoder_1_out1, decoder_1_out2, decoder_1_out3, decoder_1_out4, decoder_1_out5, decoder_1_out6,
       decoder_1_out7, decoder_1_out8, decoder_1_out9, decoder_1_out10, decoder_1_out11, decoder_1_out12,
       decoder_1_out13, decoder_1_out14, decoder_1_out15, decoder_1_out16, decoder_1_out17, decoder_1_out18,
       decoder_1_out19, decoder_1_out20, decoder_1_out21, decoder_1_out22, decoder_1_out23, decoder_1_out24,
       decoder_1_out25, decoder_1_out26, decoder_1_out27, decoder_1_out28, decoder_1_out29, decoder_1_out30,
       decoder_1_out31;
  wire [31:0] register_1_q, register_2_q, register_3_q, register_4_q, register_5_q, register_6_q,
       register_7_q, register_8_q, register_9_q, register_10_q, register_11_q, register_12_q, register_13_q,
       register_14_q, register_15_q, register_16_q, register_17_q, register_18_q, register_19_q,
       register_20_q, register_21_q, register_22_q, register_23_q, register_24_q, register_25_q,
       register_26_q, register_27_q, register_28_q, register_29_q, register_30_q, register_31_q;

  Decoder #(.enable("false"), .select(5)) decoder_1 (
    .out0(decoder_1_out0), .out1(decoder_1_out1), .out2(decoder_1_out2), .out3(decoder_1_out3),
    .out4(decoder_1_out4), .out5(decoder_1_out5), .out6(decoder_1_out6), .out7(decoder_1_out7),
    .out8(decoder_1_out8), .out9(decoder_1_out9), .out10(decoder_1_out10), .out11(decoder_1_out11),
    .out12(decoder_1_out12), .out13(decoder_1_out13), .out14(decoder_1_out14), .out15(decoder_1_out15),
    .out16(decoder_1_out16), .out17(decoder_1_out17), .out18(decoder_1_out18), .out19(decoder_1_out19),
    .out20(decoder_1_out20), .out21(decoder_1_out21), .out22(decoder_1_out22), .out23(decoder_1_out23),
    .out24(decoder_1_out24), .out25(decoder_1_out25), .out26(decoder_1_out26), .out27(decoder_1_out27),
    .out28(decoder_1_out28), .out29(decoder_1_out29), .out30(decoder_1_out30), .out31(decoder_1_out31),
    .sel(rd));
  and and_1 (and_1_out, reg_write, decoder_1_out8);
  Register #(.width(32)) register_1 (.D(write_data), .en(and_1_out), .clk(clock), .Q(register_1_q), .clr(reset));
  Register #(.width(32)) register_2 (.D(write_data), .en(and_2_out), .clk(clock), .Q(register_2_q), .clr(reset));
  and and_2 (and_2_out, reg_write, decoder_1_out16);
  and and_3 (and_3_out, reg_write, decoder_1_out24);
  Register #(.width(32)) register_3 (.D(write_data), .en(and_3_out), .clk(clock), .Q(register_3_q), .clr(reset));
  and and_4 (and_4_out, reg_write, decoder_1_out1);
  and and_5 (and_5_out, reg_write, decoder_1_out9);
  and and_6 (and_6_out, reg_write, decoder_1_out17);
  and and_7 (and_7_out, reg_write, decoder_1_out25);
  Register #(.width(32)) register_4 (.D(write_data), .en(and_4_out), .clk(clock), .Q(register_4_q), .clr(reset));
  Register #(.width(32)) register_5 (.D(write_data), .en(and_5_out), .clk(clock), .Q(register_5_q), .clr(reset));
  Register #(.width(32)) register_6 (.D(write_data), .en(and_6_out), .clk(clock), .Q(register_6_q), .clr(reset));
  Register #(.width(32)) register_7 (.D(write_data), .en(and_7_out), .clk(clock), .Q(register_7_q), .clr(reset));
  and and_8 (and_8_out, reg_write, decoder_1_out2);
  and and_9 (and_9_out, reg_write, decoder_1_out10);
  and and_10 (and_10_out, reg_write, decoder_1_out18);
  and and_11 (and_11_out, reg_write, decoder_1_out26);
  Register #(.width(32)) register_8 (.D(write_data), .en(and_8_out), .clk(clock), .Q(register_8_q), .clr(reset));
  Register #(.width(32)) register_9 (.D(write_data), .en(and_9_out), .clk(clock), .Q(register_9_q), .clr(reset));
  Register #(.width(32)) register_10 (.D(write_data), .en(and_10_out), .clk(clock), .Q(register_10_q), .clr(reset));
  Register #(.width(32)) register_11 (.D(write_data), .en(and_11_out), .clk(clock), .Q(register_11_q), .clr(reset));
  and and_12 (and_12_out, reg_write, decoder_1_out3);
  and and_13 (and_13_out, reg_write, decoder_1_out11);
  and and_14 (and_14_out, reg_write, decoder_1_out19);
  and and_15 (and_15_out, reg_write, decoder_1_out27);
  Register #(.width(32)) register_12 (.D(write_data), .en(and_12_out), .clk(clock), .Q(register_12_q), .clr(reset));
  Register #(.width(32)) register_13 (.D(write_data), .en(and_13_out), .clk(clock), .Q(register_13_q), .clr(reset));
  Register #(.width(32)) register_14 (.D(write_data), .en(and_14_out), .clk(clock), .Q(register_14_q), .clr(reset));
  Register #(.width(32)) register_15 (.D(write_data), .en(and_15_out), .clk(clock), .Q(register_15_q), .clr(reset));
  and and_16 (and_16_out, reg_write, decoder_1_out4);
  and and_17 (and_17_out, reg_write, decoder_1_out12);
  and and_18 (and_18_out, reg_write, decoder_1_out20);
  and and_19 (and_19_out, reg_write, decoder_1_out28);
  Register #(.width(32)) register_16 (.D(write_data), .en(and_16_out), .clk(clock), .Q(register_16_q), .clr(reset));
  Register #(.width(32)) register_17 (.D(write_data), .en(and_17_out), .clk(clock), .Q(register_17_q), .clr(reset));
  Register #(.width(32)) register_18 (.D(write_data), .en(and_18_out), .clk(clock), .Q(register_18_q), .clr(reset));
  Register #(.width(32)) register_19 (.D(write_data), .en(and_19_out), .clk(clock), .Q(register_19_q), .clr(reset));
  and and_20 (and_20_out, reg_write, decoder_1_out5);
  and and_21 (and_21_out, reg_write, decoder_1_out13);
  and and_22 (and_22_out, reg_write, decoder_1_out21);
  and and_23 (and_23_out, reg_write, decoder_1_out29);
  Register #(.width(32)) register_20 (.D(write_data), .en(and_20_out), .clk(clock), .Q(register_20_q), .clr(reset));
  Register #(.width(32)) register_21 (.D(write_data), .en(and_21_out), .clk(clock), .Q(register_21_q), .clr(reset));
  Register #(.width(32)) register_22 (.D(write_data), .en(and_22_out), .clk(clock), .Q(register_22_q), .clr(reset));
  Register #(.width(32)) register_23 (.D(write_data), .en(and_23_out), .clk(clock), .Q(register_23_q), .clr(reset));
  and and_24 (and_24_out, reg_write, decoder_1_out6);
  and and_25 (and_25_out, reg_write, decoder_1_out14);
  and and_26 (and_26_out, reg_write, decoder_1_out22);
  and and_27 (and_27_out, reg_write, decoder_1_out30);
  Register #(.width(32)) register_24 (.D(write_data), .en(and_24_out), .clk(clock), .Q(register_24_q), .clr(reset));
  Register #(.width(32)) register_25 (.D(write_data), .en(and_25_out), .clk(clock), .Q(register_25_q), .clr(reset));
  Register #(.width(32)) register_26 (.D(write_data), .en(and_26_out), .clk(clock), .Q(register_26_q), .clr(reset));
  Register #(.width(32)) register_27 (.D(write_data), .en(and_27_out), .clk(clock), .Q(register_27_q), .clr(reset));
  and and_28 (and_28_out, reg_write, decoder_1_out7);
  and and_29 (and_29_out, reg_write, decoder_1_out15);
  and and_30 (and_30_out, reg_write, decoder_1_out23);
  and and_31 (and_31_out, reg_write, decoder_1_out31);
  Register #(.width(32)) register_28 (.D(write_data), .en(and_28_out), .clk(clock), .Q(register_28_q), .clr(reset));
  Register #(.width(32)) register_29 (.D(write_data), .en(and_29_out), .clk(clock), .Q(register_29_q), .clr(reset));
  Register #(.width(32)) register_30 (.D(write_data), .en(and_30_out), .clk(clock), .Q(register_30_q), .clr(reset));
  Register #(.width(32)) register_31 (.D(write_data), .en(and_31_out), .clk(clock), .Q(register_31_q), .clr(reset));
  Multiplexer #(.select(5), .width(32)) multiplexer_1 (
    .in0({32{1'b0}}), .in1(register_4_q), .in2(register_8_q), .in3(register_12_q), .in4(register_16_q),
    .in5(register_20_q), .in6(register_24_q), .in7(register_28_q), .in8(register_1_q), .in9(register_5_q),
    .in10(register_9_q), .in11(register_13_q), .in12(register_17_q), .in13(register_21_q),
    .in14(register_25_q), .in15(register_29_q), .in16(register_2_q), .in17(register_6_q),
    .in18(register_10_q), .in19(register_14_q), .in20(register_18_q), .in21(register_22_q),
    .in22(register_26_q), .in23(register_30_q), .in24(register_3_q), .in25(register_7_q),
    .in26(register_11_q), .in27(register_15_q), .in28(register_19_q), .in29(register_23_q),
    .in30(register_27_q), .in31(register_31_q), .out(read_data_2), .sel(rs2));
  Multiplexer #(.select(5), .width(32)) multiplexer_2 (
    .in0({32{1'b0}}), .in1(register_4_q), .in2(register_8_q), .in3(register_12_q), .in4(register_16_q),
    .in5(register_20_q), .in6(register_24_q), .in7(register_28_q), .in8(register_1_q), .in9(register_5_q),
    .in10(register_9_q), .in11(register_13_q), .in12(register_17_q), .in13(register_21_q),
    .in14(register_25_q), .in15(register_29_q), .in16(register_2_q), .in17(register_6_q),
    .in18(register_10_q), .in19(register_14_q), .in20(register_18_q), .in21(register_22_q),
    .in22(register_26_q), .in23(register_30_q), .in24(register_3_q), .in25(register_7_q),
    .in26(register_11_q), .in27(register_15_q), .in28(register_19_q), .in29(register_23_q),
    .in30(register_27_q), .in31(register_31_q), .out(read_data_1), .sel(rs1));
endmodule

module ImmediateGen (
  input  [31:0] instruction,
  output [31:0] immediate
);

  wire comparator_2_eq, comparator_3_eq, comparator_4_eq;
  wire [2:0] or_2_out;
  wire [31:0] bit_extender_1_out, bit_extender_2_out, bit_extender_3_out, bit_extender_4_out;

  Comparator #(.mode("unsigned"), .width(7)) comparator_1 (
    .a(7'b1101111), .b(instruction[6:0]), .eq(or_2_out[2]));  // open: gt, lt
  Comparator #(.mode("unsigned"), .width(7)) comparator_2 (
    .a(7'b1100011), .b(instruction[6:0]), .eq(comparator_2_eq));  // open: gt, lt
  Comparator #(.mode("unsigned"), .width(7)) comparator_3 (
    .a(7'b0110111), .b(instruction[6:0]), .eq(comparator_3_eq));  // open: gt, lt
  Comparator #(.mode("unsigned"), .width(7)) comparator_4 (
    .a(7'b0100011), .b(instruction[6:0]), .eq(comparator_4_eq));  // open: gt, lt
  assign bit_extender_1_out = {{20{instruction[31]}}, instruction[31:20]};  // Bit_Extender bit_extender_1
  assign bit_extender_2_out = {{20{instruction[31]}}, {instruction[31:25], instruction[11:7]}};  // Bit_Extender bit_extender_2
  assign bit_extender_3_out = {{19{instruction[31]}}, {instruction[31], instruction[7], instruction[30:25], instruction[11:8], 1'b0}};  // Bit_Extender bit_extender_3
  assign bit_extender_4_out = {{11{instruction[31]}}, {instruction[31], instruction[19:12], instruction[20], instruction[30:21], 1'b0}};  // Bit_Extender bit_extender_4
  or or_1 (or_2_out[1], comparator_2_eq, comparator_3_eq);
  or or_2 (or_2_out[0], comparator_3_eq, comparator_4_eq);
  Multiplexer #(.select(3), .width(32)) multiplexer_1 (
    .in0(bit_extender_1_out), .in1(bit_extender_2_out), .in2(bit_extender_3_out),
    .in3({instruction[31:12], {12{1'b0}}}), .in4(bit_extender_4_out), .out(immediate), .sel(or_2_out));  // open: in5, in6, in7
endmodule

module ControlUnit (
  input  [6:0] opcode,
  output [1:0] result_src,
  output alu_src,
  output mem_read,
  output reg_write,
  output branch,
  output mem_write,
  output alu_sub,
  output jump,
  output jalr
);

  wire comparator_1_eq, comparator_2_eq, comparator_6_eq, comparator_7_eq;

  Comparator #(.mode("unsigned"), .width(7)) comparator_1 (
    .a(7'b0110011), .b(opcode), .eq(comparator_1_eq));  // open: gt, lt
  Comparator #(.mode("unsigned"), .width(7)) comparator_2 (
    .a(7'b0010011), .b(opcode), .eq(comparator_2_eq));  // open: gt, lt
  Comparator #(.mode("unsigned"), .width(7)) comparator_3 (.a(7'b0000011), .b(opcode), .eq(mem_read));  // open: gt, lt
  Comparator #(.mode("unsigned"), .width(7)) comparator_4 (.a(7'b0100011), .b(opcode), .eq(mem_write));  // open: gt, lt
  Comparator #(.mode("unsigned"), .width(7)) comparator_5 (.a(7'b1100011), .b(opcode), .eq(alu_sub));  // open: gt, lt
  Comparator #(.mode("unsigned"), .width(7)) comparator_6 (
    .a(7'b0110111), .b(opcode), .eq(comparator_6_eq));  // open: gt, lt
  Comparator #(.mode("unsigned"), .width(7)) comparator_7 (
    .a(7'b1101111), .b(opcode), .eq(comparator_7_eq));  // open: gt, lt
  Comparator #(.mode("unsigned"), .width(7)) comparator_8 (.a(7'b1100111), .b(opcode), .eq(jalr));  // open: gt, lt
  or or_1 (result_src[0], jump, mem_read);
  or or_2 (alu_src, comparator_2_eq, mem_read, mem_write, jalr);
  or or_3 (reg_write, comparator_1_eq, comparator_2_eq, mem_read, comparator_6_eq, comparator_7_eq, jalr);
  or or_4 (result_src[1], comparator_6_eq, jump);
  or or_5 (jump, comparator_7_eq, jalr);

  assign branch = alu_sub;
endmodule

module ID_EX (
  input  [31:0] pc,
  input  [31:0] read_data_1,
  input  [31:0] read_data_2,
  input  [31:0] immediate,
  input  [4:0] rd,
  input  [4:0] rs1,
  input  [4:0] rs2,
  input  [2:0] funct3,
  input  [6:0] funct7,
  input  [1:0] result_src,
  input  alu_src,
  input  mem_read,
  input  mem_write,
  input  reg_write,
  input  branch,
  input  alu_sub,
  input  jump,
  input  jalr,
  input  reset,
  input  clock,
  input  enable,
  output [31:0] ex_pc,
  output [31:0] ex_read_data_1,
  output [31:0] ex_read_data_2,
  output [31:0] ex_immediate,
  output [4:0] ex_rd,
  output [4:0] ex_rs1,
  output [4:0] ex_rs2,
  output [2:0] ex_funct3,
  output [6:0] ex_funct7,
  output [1:0] ex_result_src,
  output ex_alu_src,
  output ex_mem_read,
  output ex_mem_write,
  output ex_reg_write,
  output ex_branch,
  output ex_alu_sub,
  output ex_jump,
  output ex_jalr
);

  Register #(.width(32)) register_1 (.D(pc), .en(enable), .clk(clock), .Q(ex_pc), .clr(reset));
  Register #(.width(32)) register_2 (.D(read_data_1), .en(enable), .clk(clock), .Q(ex_read_data_1), .clr(reset));
  Register #(.width(32)) register_3 (.D(read_data_2), .en(enable), .clk(clock), .Q(ex_read_data_2), .clr(reset));
  Register #(.width(32)) register_4 (.D(immediate), .en(enable), .clk(clock), .Q(ex_immediate), .clr(reset));
  Register #(.width(5)) register_5 (.D(rd), .en(enable), .clk(clock), .Q(ex_rd), .clr(reset));
  Register #(.width(5)) register_6 (.D(rs1), .en(enable), .clk(clock), .Q(ex_rs1), .clr(reset));
  Register #(.width(1)) register_7 (.D(jump), .en(enable), .clk(clock), .Q(ex_jump), .clr(reset));
  Register #(.width(1)) register_8 (.D(jalr), .en(enable), .clk(clock), .Q(ex_jalr), .clr(reset));
  Register #(.width(5)) register_9 (.D(rs2), .en(enable), .clk(clock), .Q(ex_rs2), .clr(reset));
  Register #(.width(1)) register_10 (.D(alu_sub), .en(enable), .clk(clock), .Q(ex_alu_sub), .clr(reset));
  Register #(.width(3)) register_11 (.D(funct3), .en(enable), .clk(clock), .Q(ex_funct3), .clr(reset));
  Register #(.width(1)) register_12 (.D(branch), .en(enable), .clk(clock), .Q(ex_branch), .clr(reset));
  Register #(.width(7)) register_13 (.D(funct7), .en(enable), .clk(clock), .Q(ex_funct7), .clr(reset));
  Register #(.width(1)) register_14 (.D(reg_write), .en(enable), .clk(clock), .Q(ex_reg_write), .clr(reset));
  Register #(.width(2)) register_15 (.D(result_src), .en(enable), .clk(clock), .Q(ex_result_src), .clr(reset));
  Register #(.width(1)) register_16 (.D(mem_write), .en(enable), .clk(clock), .Q(ex_mem_write), .clr(reset));
  Register #(.width(1)) register_17 (.D(alu_src), .en(enable), .clk(clock), .Q(ex_alu_src), .clr(reset));
  Register #(.width(1)) register_18 (.D(mem_read), .en(enable), .clk(clock), .Q(ex_mem_read), .clr(reset));
endmodule

module Execute (
  input  jump,
  input  jalr,
  input  branch,
  input  [31:0] pc,
  input  [31:0] read_data_1,
  input  [31:0] read_data_2,
  input  [31:0] immediate,
  input  alu_src,
  input  alu_sub,
  output [31:0] br_target,
  output br_taken,
  output [31:0] result,
  output zero
);

  wire and_2_out;
  wire [31:0] adder_1_out, adder_2_out, and_1_out, multiplexer_1_out;

  Multiplexer #(.width(32)) multiplexer_1 (.in0(read_data_2), .in1(immediate), .out(multiplexer_1_out), .sel(alu_src));
  Adder #(.width(32)) adder_1 (.a(immediate), .b(read_data_1), .out(adder_1_out));  // open: cin, cout
  Adder #(.width(32)) adder_2 (.a(pc), .b(immediate), .out(adder_2_out));  // open: cin, cout
  assign and_1_out = 32'hfffffffe & adder_1_out;  // AND_Gate and_1, 32 bits wide
  and and_2 (and_2_out, branch, zero);
  Multiplexer #(.width(32)) multiplexer_2 (.in0(adder_2_out), .in1(and_1_out), .out(br_target), .sel(jalr));
  or or_1 (br_taken, jump, and_2_out);
  ALU Alu1 (.A(read_data_1), .B(multiplexer_1_out), .Operation({1'b0, alu_sub}), .result(result), .zero(zero));
endmodule

module ALU (
  input  [31:0] A,
  input  [31:0] B,
  input  [1:0] Operation,
  output [31:0] result,
  output zero
);

  wire [31:0] adder_1_out, and_1_out, or_1_out, subtractor_1_out;

  Adder #(.width(32)) adder_1 (.a(A), .b(B), .out(adder_1_out));  // open: cin, cout
  Subtractor #(.width(32)) subtractor_1 (.a(A), .b(B), .out(subtractor_1_out));  // open: bin, bout
  assign and_1_out = A & B;  // AND_Gate and_1, 32 bits wide
  assign or_1_out = A | B;  // OR_Gate or_1, 32 bits wide
  Multiplexer #(.select(2), .width(32)) multiplexer_1 (
    .in0(adder_1_out), .in1(subtractor_1_out), .in2(and_1_out), .in3(or_1_out), .out(result), .sel(Operation));
  Comparator #(.mode("unsigned"), .width(32)) comparator_1 (.a(result), .b({32{1'b0}}), .eq(zero));  // open: gt, lt
endmodule

module EX_MEM (
  input  [31:0] pc,
  input  [31:0] alu_result,
  input  [31:0] read_data_2,
  input  [4:0] rd,
  input  [31:0] immediate,
  input  [1:0] result_src,
  input  mem_read,
  input  mem_write,
  input  reg_write,
  input  jump,
  input  [4:0] ex_rs2,
  input  reset,
  input  clock,
  input  enable,
  output [31:0] mem_pc,
  output [31:0] mem_alu_result,
  output [31:0] mem_read_data_2,
  output [4:0] mem_rd,
  output [31:0] mem_immediate,
  output [1:0] mem_result_src,
  output mem_mem_read,
  output mem_mem_write,
  output mem_reg_write,
  output mem_jump,
  output [4:0] mem_rs2
);

  Register #(.width(32)) register_1 (.D(pc), .en(enable), .clk(clock), .Q(mem_pc), .clr(reset));
  Register #(.width(32)) register_2 (.D(alu_result), .en(enable), .clk(clock), .Q(mem_alu_result), .clr(reset));
  Register #(.width(32)) register_3 (.D(read_data_2), .en(enable), .clk(clock), .Q(mem_read_data_2), .clr(reset));
  Register #(.width(5)) register_4 (.D(rd), .en(enable), .clk(clock), .Q(mem_rd), .clr(reset));
  Register #(.width(32)) register_5 (.D(immediate), .en(enable), .clk(clock), .Q(mem_immediate), .clr(reset));
  Register #(.width(2)) register_6 (.D(result_src), .en(enable), .clk(clock), .Q(mem_result_src), .clr(reset));
  Register #(.width(1)) register_7 (.D(mem_read), .en(enable), .clk(clock), .Q(mem_mem_read));  // open: clr
  Register #(.width(1)) register_8 (.D(mem_write), .en(enable), .clk(clock), .Q(mem_mem_write), .clr(reset));
  Register #(.width(1)) register_9 (.D(reg_write), .en(enable), .clk(clock), .Q(mem_reg_write), .clr(reset));
  Register #(.width(1)) register_10 (.D(jump), .en(enable), .clk(clock), .Q(mem_jump), .clr(reset));
  Register #(.width(5)) register_11 (.D(ex_rs2), .en(enable), .clk(clock), .Q(mem_rs2), .clr(reset));
endmodule

module Memory (
  input  [31:0] address,
  input  mem_write,
  input  mem_read,
  input  clock,
  input  [31:0] write_data,
  output [31:0] read_data
);

  RAM #(.asyncread("true"), .dataWidth(32)) DataRam1 (
    .addr(address[9:2]), .we(mem_write), .oe(mem_read), .clk(clock), .din(write_data), .dout(read_data));
endmodule

module MEM_WB (
  input  [31:0] pc,
  input  [31:0] alu_result,
  input  [31:0] read_data,
  input  [4:0] rd,
  input  [31:0] immediate,
  input  [1:0] result_src,
  input  reg_write,
  input  reset,
  input  clock,
  input  enable,
  output [31:0] wb_pc,
  output [31:0] wb_data,
  output [31:0] wb_alu_result,
  output [31:0] wb_read_data,
  output [4:0] wb_rd,
  output [31:0] wb_immediate,
  output [1:0] wb_result_src,
  output wb_reg_write
);

  wire [31:0] adder_1_out;

  Register #(.width(32)) register_1 (.D(pc), .en(enable), .clk(clock), .Q(wb_pc), .clr(reset));
  Register #(.width(32)) register_2 (.D(alu_result), .en(enable), .clk(clock), .Q(wb_alu_result), .clr(reset));
  Register #(.width(32)) register_3 (.D(read_data), .en(enable), .clk(clock), .Q(wb_read_data), .clr(reset));
  Register #(.width(5)) register_4 (.D(rd), .en(enable), .clk(clock), .Q(wb_rd), .clr(reset));
  Register #(.width(32)) register_5 (.D(immediate), .en(enable), .clk(clock), .Q(wb_immediate), .clr(reset));
  Register #(.width(2)) register_6 (.D(result_src), .en(enable), .clk(clock), .Q(wb_result_src), .clr(reset));
  Register #(.width(1)) register_7 (.D(reg_write), .en(enable), .clk(clock), .Q(wb_reg_write), .clr(reset));
  Adder #(.width(32)) adder_1 (.a(32'h4), .b(wb_pc), .out(adder_1_out));  // open: cin, cout
  Multiplexer #(.select(2), .width(32)) multiplexer_1 (
    .in0(wb_alu_result), .in1(wb_read_data), .in2(wb_immediate), .in3(adder_1_out), .out(wb_data),
    .sel(wb_result_src));
endmodule

module ForwardingUnit (
  input  [31:0] ex_read_data_2,
  input  [4:0] wb_rd,
  input  [31:0] ex_read_data_1,
  input  wb_reg_write,
  input  [31:0] wb_data,
  input  [4:0] ex_rs1,
  input  [4:0] ex_rs2,
  input  [4:0] mem_rd,
  input  [31:0] mem_alu_result,
  input  mem_reg_write,
  input  mem_mem_read,
  output [31:0] read_data_1,
  output [31:0] read_data_2,
  output [4:0] ex_rs2_op
);

  wire and_1_out, and_2_out, and_3_out, and_4_out, and_5_out, and_6_out, comparator_1_eq, comparator_2_eq,
       comparator_3_eq, comparator_4_eq, comparator_5_eq, comparator_6_eq, not_1_out, not_2_out, not_3_out;
  wire [31:0] multiplexer_1_out, multiplexer_3_out;

  Comparator #(.mode("unsigned"), .width(5)) comparator_1 (
    .a(wb_rd), .b(ex_rs1), .eq(comparator_1_eq));  // open: gt, lt
  Comparator #(.mode("unsigned"), .width(5)) comparator_2 (
    .a(ex_rs1), .b(mem_rd), .eq(comparator_2_eq));  // open: gt, lt
  and and_1 (and_1_out, and_5_out, comparator_1_eq);
  and and_2 (and_2_out, and_6_out, comparator_2_eq);
  Multiplexer #(.width(32)) multiplexer_1 (
    .in0(ex_read_data_1), .in1(wb_data), .out(multiplexer_1_out), .sel(and_1_out));
  Multiplexer #(.width(32)) multiplexer_2 (
    .in0(multiplexer_1_out), .in1(mem_alu_result), .out(read_data_1), .sel(and_2_out));
  Comparator #(.mode("unsigned"), .width(5)) comparator_3 (
    .a(wb_rd), .b(ex_rs2), .eq(comparator_3_eq));  // open: gt, lt
  Multiplexer #(.width(32)) multiplexer_3 (
    .in0(ex_read_data_2), .in1(wb_data), .out(multiplexer_3_out), .sel(and_3_out));
  and and_3 (and_3_out, comparator_3_eq, and_5_out);
  and and_4 (and_4_out, and_6_out, comparator_4_eq);
  Comparator #(.mode("unsigned"), .width(5)) comparator_4 (
    .a(ex_rs2), .b(mem_rd), .eq(comparator_4_eq));  // open: gt, lt
  Multiplexer #(.width(32)) multiplexer_4 (
    .in0(multiplexer_3_out), .in1(mem_alu_result), .out(read_data_2), .sel(and_4_out));
  Comparator #(.mode("unsigned"), .width(5)) comparator_5 (
    .a({5{1'b0}}), .b(wb_rd), .eq(comparator_5_eq));  // open: gt, lt
  Comparator #(.mode("unsigned"), .width(5)) comparator_6 (
    .a({5{1'b0}}), .b(mem_rd), .eq(comparator_6_eq));  // open: gt, lt
  not not_1 (not_1_out, comparator_5_eq);
  not not_2 (not_2_out, comparator_6_eq);
  not not_3 (not_3_out, mem_mem_read);
  and and_5 (and_5_out, not_1_out, wb_reg_write);
  and and_6 (and_6_out, not_2_out, mem_reg_write, not_3_out);

  assign ex_rs2_op = ex_rs2;
endmodule

module HarzardDetectionUnit (
  input  [4:0] ex_rd,
  input  [4:0] rs1,
  input  [4:0] rs2,
  input  ex_mem_read,
  output stall
);

  wire comparator_1_eq, comparator_2_eq, comparator_3_eq, not_1_out, or_1_out;

  Comparator #(.width(5)) comparator_1 (.a({5{1'b0}}), .b(ex_rd), .eq(comparator_1_eq));  // open: gt, lt
  Comparator #(.width(5)) comparator_2 (.a(rs1), .b(ex_rd), .eq(comparator_2_eq));  // open: gt, lt
  Comparator #(.width(5)) comparator_3 (.a(rs2), .b(ex_rd), .eq(comparator_3_eq));  // open: gt, lt
  not not_1 (not_1_out, comparator_1_eq);
  or or_1 (or_1_out, comparator_2_eq, comparator_3_eq);
  and and_1 (stall, not_1_out, or_1_out, ex_mem_read);
endmodule

module BubbleControl (
  input  jalr,
  input  reg_write,
  input  mem_read,
  input  mem_write,
  input  branch,
  input  jump,
  input  not_stall,
  output jalr_op,
  output reg_write_op,
  output mem_read_op,
  output mem_write_op,
  output branch_op,
  output jump_op
);

  and and_1 (jalr_op, jalr, not_stall);
  and and_2 (reg_write_op, reg_write, not_stall);
  and and_3 (mem_read_op, mem_read, not_stall);
  and and_4 (mem_write_op, mem_write, not_stall);
  and and_5 (branch_op, branch, not_stall);
  and and_6 (jump_op, jump, not_stall);
endmodule

module StoreForwardingUnit (
  input  [31:0] mem_read_data_2,
  input  [31:0] wb_data,
  input  mem_mem_write,
  input  wb_reg_write,
  input  [4:0] wb_rd,
  input  [4:0] mem_rs2,
  output [31:0] mem_store_data
);

  wire and_1_out, comparator_1_eq, comparator_2_eq, not_1_out;

  Comparator #(.width(5)) comparator_1 (.a(wb_rd), .b({5{1'b0}}), .eq(comparator_1_eq));  // open: gt, lt
  Comparator #(.width(5)) comparator_2 (.a(wb_rd), .b(mem_rs2), .eq(comparator_2_eq));  // open: gt, lt
  not not_1 (not_1_out, comparator_1_eq);
  and and_1 (and_1_out, mem_mem_write, wb_reg_write, not_1_out, comparator_2_eq);
  Multiplexer #(.width(32)) multiplexer_1 (.in0(mem_read_data_2), .in1(wb_data), .out(mem_store_data), .sel(and_1_out));
endmodule
