// Logisim project tinyGpu.circ as structural Verilog
module ALU (
  input  [2:0] core_state,
  input  enable,
  input  [7:0] rs,
  input  reset,
  input  [7:0] rt,
  input  d_alu_output_mux,
  input  clock,
  input  [1:0] d_alu_arithmetic_mux,
  output [7:0] alu_out
);

  wire and_1_out, comparator_2_eq;
  wire [2:0] comparator_1_lt;
  wire [7:0] adder_1_out, divider_1_out, multiplexer_1_out, multiplexer_2_out, multiplier_1_out,
       subtractor_1_out;

  Adder adder_1 (.a(rs), .b(rt), .out(adder_1_out));  // open: cin, cout
  Subtractor subtractor_1 (.a(rs), .b(rt), .out(subtractor_1_out));  // open: bin, bout
  Multiplier multiplier_1 (.a(rs), .b(rt), .out(multiplier_1_out));  // open: cin, cout
  Divider divider_1 (.a(rs), .b(rt), .out(divider_1_out));  // open: upper, rem
  Multiplexer #(.select(2), .width(8)) multiplexer_1 (
    .in0(adder_1_out), .in1(subtractor_1_out), .in2(multiplier_1_out), .in3(divider_1_out),
    .out(multiplexer_1_out), .sel(d_alu_arithmetic_mux));
  Comparator comparator_1 (
    .a(multiplexer_1_out), .b({8{1'b0}}), .gt(comparator_1_lt[2]), .eq(comparator_1_lt[1]),
    .lt(comparator_1_lt[0]));
  Comparator #(.mode("unsigned"), .width(3)) comparator_2 (
    .a(core_state), .b(3'b101), .eq(comparator_2_eq));  // open: gt, lt
  and and_1 (and_1_out, comparator_2_eq, enable);
  Multiplexer #(.width(8)) multiplexer_2 (
    .in0(multiplexer_1_out), .in1({{5{1'b0}}, comparator_1_lt}), .out(multiplexer_2_out),
    .sel(d_alu_output_mux));
  Register register_1 (.D(multiplexer_2_out), .en(and_1_out), .clk(clock), .Q(alu_out), .clr(reset));
endmodule

module Registers (
  input  [3:0] d_rt_address,
  input  [3:0] d_rs_address,
  input  reset,
  input  [7:0] blockDim,
  input  [7:0] threadIdx,
  input  [7:0] alu_out,
  input  [7:0] lsu_out,
  input  [7:0] blockId,
  input  [7:0] d_immediate,
  input  [1:0] d_r_in_mux,
  input  clock,
  input  enable,
  input  [2:0] core_state,
  input  d_r_wr_enable,
  input  [3:0] d_rd_address,
  output [7:0] rt_op,
  output [7:0] rs_op
);

  wire and_1_out, and_2_out, and_3_out, and_4_out, and_5_out, and_6_out, and_7_out, and_8_out, and_9_out,
       and_10_out, and_11_out, and_12_out, and_13_out, and_14_out, and_15_out, and_16_out, and_17_out,
       and_18_out, comparator_1_eq, comparator_2_eq, decoder_1_out0, decoder_1_out1, decoder_1_out2,
       decoder_1_out3, decoder_1_out4, decoder_1_out5, decoder_1_out6, decoder_1_out7, decoder_1_out8,
       decoder_1_out9, decoder_1_out10, decoder_1_out11, decoder_1_out12, decoder_1_out13, decoder_1_out14,
       decoder_1_out15;
  wire [7:0] multiplexer_1_out, multiplexer_2_out, multiplexer_3_out, register_1_q, register_2_q,
       register_3_q, register_4_q, register_5_q, register_6_q, register_7_q, register_8_q, register_9_q,
       register_10_q, register_11_q, register_12_q, register_13_q, register_14_q;

  Decoder #(.enable("false"), .select(4)) decoder_1 (
    .out0(decoder_1_out0), .out1(decoder_1_out1), .out2(decoder_1_out2), .out3(decoder_1_out3),
    .out4(decoder_1_out4), .out5(decoder_1_out5), .out6(decoder_1_out6), .out7(decoder_1_out7),
    .out8(decoder_1_out8), .out9(decoder_1_out9), .out10(decoder_1_out10), .out11(decoder_1_out11),
    .out12(decoder_1_out12), .out13(decoder_1_out13), .out14(decoder_1_out14), .out15(decoder_1_out15),
    .sel(d_rd_address));
  Multiplexer #(.select(2), .width(8)) multiplexer_1 (
    .in0(alu_out), .in1(lsu_out), .in2(d_immediate), .out(multiplexer_1_out), .sel(d_r_in_mux));  // open: in3
  and and_1 (and_1_out, enable, comparator_1_eq);
  Comparator #(.mode("unsigned"), .width(3)) comparator_1 (
    .a(3'b011), .b(core_state), .eq(comparator_1_eq));  // open: gt, lt
  Comparator #(.mode("unsigned"), .width(3)) comparator_2 (
    .a(core_state), .b(3'b110), .eq(comparator_2_eq));  // open: gt, lt
  and and_2 (and_2_out, enable, comparator_2_eq);
  and and_3 (and_3_out, d_r_wr_enable, and_2_out, decoder_1_out0);
  Register register_1 (.D(multiplexer_1_out), .en(and_3_out), .clk(clock), .Q(register_1_q), .clr(reset));
  Register register_2 (.D(multiplexer_1_out), .en(and_4_out), .clk(clock), .Q(register_2_q), .clr(reset));
  and and_4 (and_4_out, d_r_wr_enable, and_2_out, decoder_1_out8);
  and and_5 (and_5_out, d_r_wr_enable, and_2_out, decoder_1_out1);
  and and_6 (and_6_out, d_r_wr_enable, and_2_out, decoder_1_out9);
  Register register_3 (.D(multiplexer_1_out), .en(and_5_out), .clk(clock), .Q(register_3_q), .clr(reset));
  Register register_4 (.D(multiplexer_1_out), .en(and_6_out), .clk(clock), .Q(register_4_q), .clr(reset));
  and and_7 (and_7_out, d_r_wr_enable, and_2_out, decoder_1_out2);
  and and_8 (and_8_out, d_r_wr_enable, and_2_out, decoder_1_out10);
  Register register_5 (.D(multiplexer_1_out), .en(and_7_out), .clk(clock), .Q(register_5_q), .clr(reset));
  Register register_6 (.D(multiplexer_1_out), .en(and_8_out), .clk(clock), .Q(register_6_q), .clr(reset));
  and and_9 (and_9_out, d_r_wr_enable, and_2_out, decoder_1_out3);
  and and_10 (and_10_out, d_r_wr_enable, and_2_out, decoder_1_out11);
  Register register_7 (.D(multiplexer_1_out), .en(and_9_out), .clk(clock), .Q(register_7_q), .clr(reset));
  Register register_8 (.D(multiplexer_1_out), .en(and_10_out), .clk(clock), .Q(register_8_q), .clr(reset));
  and and_11 (and_11_out, d_r_wr_enable, and_2_out, decoder_1_out4);
  and and_12 (and_12_out, d_r_wr_enable, and_2_out, decoder_1_out12);
  Register register_9 (.D(multiplexer_1_out), .en(and_11_out), .clk(clock), .Q(register_9_q), .clr(reset));
  Register register_10 (.D(multiplexer_1_out), .en(and_12_out), .clk(clock), .Q(register_10_q), .clr(reset));
  and and_13 (and_13_out, d_r_wr_enable, and_2_out, decoder_1_out5);
  and and_14 (and_14_out, d_r_wr_enable, and_2_out, decoder_1_out13);
  Register register_11 (.D(multiplexer_1_out), .en(and_13_out), .clk(clock), .Q(register_11_q), .clr(reset));
  Register register_12 (.D(blockId), .en(enable), .clk(clock), .Q(register_12_q), .clr(reset));
  and and_15 (and_15_out, d_r_wr_enable, and_2_out, decoder_1_out6);
  and and_16 (and_16_out, d_r_wr_enable, and_2_out, decoder_1_out14);
  Register register_13 (.D(multiplexer_1_out), .en(and_15_out), .clk(clock), .Q(register_13_q), .clr(reset));
  and and_17 (and_17_out, d_r_wr_enable, and_2_out, decoder_1_out7);
  and and_18 (and_18_out, d_r_wr_enable, and_2_out, decoder_1_out15);
  Register register_14 (.D(multiplexer_1_out), .en(and_17_out), .clk(clock), .Q(register_14_q), .clr(reset));
  Multiplexer #(.select(4), .width(8)) multiplexer_2 (
    .in0(register_1_q), .in1(register_3_q), .in2(register_5_q), .in3(register_7_q), .in4(register_9_q),
    .in5(register_11_q), .in6(register_13_q), .in7(register_14_q), .in8(register_2_q), .in9(register_4_q),
    .in10(register_6_q), .in11(register_8_q), .in12(register_10_q), .in13(register_12_q), .in14(blockDim),
    .in15(threadIdx), .out(multiplexer_2_out), .sel(d_rt_address));
  Multiplexer #(.select(4), .width(8)) multiplexer_3 (
    .in0(register_1_q), .in1(register_3_q), .in2(register_5_q), .in3(register_7_q), .in4(register_9_q),
    .in5(register_11_q), .in6(register_13_q), .in7(register_14_q), .in8(register_2_q), .in9(register_4_q),
    .in10(register_6_q), .in11(register_8_q), .in12(register_10_q), .in13(register_12_q), .in14(blockDim),
    .in15(threadIdx), .out(multiplexer_3_out), .sel(d_rs_address));
  Register rt (.D(multiplexer_2_out), .en(and_1_out), .clk(clock), .Q(rt_op), .clr(reset));
  Register rs (.D(multiplexer_3_out), .en(and_1_out), .clk(clock), .Q(rs_op), .clr(reset));
endmodule

module PC (
  input  enable,
  input  [7:0] current_pc,
  input  [7:0] d_immediate,
  input  [2:0] d_nzp,
  input  [7:0] alu_out,
  input  d_pc_mux,
  input  clock,
  input  reset,
  input  [2:0] core_state,
  input  d_nzp_wr_enable,
  output [7:0] next_pc_op
);

  wire and_1_out, and_2_out, and_4_out, comparator_1_eq, comparator_2_eq, comparator_3_gt;
  wire [2:0] and_3_out, nzp_q;
  wire [7:0] adder_1_out, multiplexer_1_out;

  Comparator #(.mode("unsigned"), .width(3)) comparator_1 (
    .a(core_state), .b(3'b101), .eq(comparator_1_eq));  // open: gt, lt
  and and_1 (and_1_out, enable, comparator_1_eq);
  Comparator #(.mode("unsigned"), .width(3)) comparator_2 (
    .a(core_state), .b(3'b110), .eq(comparator_2_eq));  // open: gt, lt
  and and_2 (and_2_out, comparator_2_eq, enable, d_nzp_wr_enable);
  Register #(.width(3)) nzp (.D(alu_out[2:0]), .en(and_2_out), .clk(clock), .Q(nzp_q), .clr(reset));
  assign and_3_out = d_nzp & nzp_q;  // AND_Gate and_3, 3 bits wide
  Adder adder_1 (.a(current_pc), .b(8'h1), .out(adder_1_out));  // open: cin, cout
  Multiplexer #(.width(8)) multiplexer_1 (
    .in0(adder_1_out), .in1(d_immediate), .out(multiplexer_1_out), .sel(and_4_out));
  Comparator #(.mode("unsigned"), .width(3)) comparator_3 (
    .a(and_3_out), .b(3'b000), .gt(comparator_3_gt));  // open: eq, lt
  and and_4 (and_4_out, comparator_3_gt, d_pc_mux);
  Register next_pc (.D(multiplexer_1_out), .en(and_1_out), .clk(clock), .Q(next_pc_op), .clr(reset));
endmodule

module DCR (
  input  [7:0] d_ctl_data,
  input  d_ctl_wr_enable,
  input  clock,
  input  reset,
  output [7:0] thread_count
);

  Register register_1 (.D(d_ctl_data), .en(d_ctl_wr_enable), .clk(clock), .Q(thread_count), .clr(reset));
endmodule

module InstDecode (
  input  [15:0] instruction,
  input  clock,
  input  reset,
  input  [2:0] core_state,
  output [3:0] d_rd_address_op,
  output [3:0] d_rs_address_op,
  output [3:0] d_rt_address_op,
  output [2:0] d_nzp_op,
  output [7:0] d_immediate_op,
  output d_r_wr_enable_op,
  output d_m_rd_enable_op,
  output d_m_wr_enable_op,
  output d_nzp_write_enable_op,
  output [1:0] d_r_inp_mux_op,
  output [1:0] d_alu_arithmetic_mux_op,
  output d_alu_output_mux_op,
  output d_pc_mux_op,
  output d_ret_op
);

  wire comparator_1_eq, instcontrollogic_1_alu_op_mux, instcontrollogic_1_mem_read,
       instcontrollogic_1_mem_write, instcontrollogic_1_nzp_write, instcontrollogic_1_pc_mux,
       instcontrollogic_1_reg_write, instcontrollogic_1_ret;
  wire [1:0] instcontrollogic_1_alu_arithmetic_mux, instcontrollogic_1_reg_input_mux;

  Comparator #(.mode("unsigned"), .width(3)) comparator_1 (
    .a(core_state), .b(3'b010), .eq(comparator_1_eq));  // open: gt, lt
  Register #(.width(1)) decoded_ret (
    .D(instcontrollogic_1_ret), .en(comparator_1_eq), .clk(clock), .Q(d_ret_op), .clr(reset));
  Register #(.width(4)) decoded_rd_address (
    .D(instruction[11:8]), .en(comparator_1_eq), .clk(clock), .Q(d_rd_address_op), .clr(reset));
  Register #(.width(1)) decoded_pc_mux (
    .D(instcontrollogic_1_pc_mux), .en(comparator_1_eq), .clk(clock), .Q(d_pc_mux_op), .clr(reset));
  Register #(.width(4)) decoded_rs_address (
    .D(instruction[7:4]), .en(comparator_1_eq), .clk(clock), .Q(d_rs_address_op), .clr(reset));
  Register #(.width(1)) decoded_alu_output_mux (
    .D(instcontrollogic_1_alu_op_mux), .en(comparator_1_eq), .clk(clock), .Q(d_alu_output_mux_op), .clr(reset));
  Register #(.width(4)) decoded_rt_address (
    .D(instruction[3:0]), .en(comparator_1_eq), .clk(clock), .Q(d_rt_address_op), .clr(reset));
  Register #(.width(2)) decoded_alu_arithmetic_mux (
    .D(instcontrollogic_1_alu_arithmetic_mux), .en(comparator_1_eq), .clk(clock),
    .Q(d_alu_arithmetic_mux_op), .clr(reset));
  Register #(.width(3)) decoded_nzp (
    .D(instruction[11:9]), .en(comparator_1_eq), .clk(clock), .Q(d_nzp_op), .clr(reset));
  Register #(.width(2)) decoded_reg_input_mux (
    .D(instcontrollogic_1_reg_input_mux), .en(comparator_1_eq), .clk(clock), .Q(d_r_inp_mux_op), .clr(reset));
  Register decoded_immediate (.D(instruction[7:0]), .en(comparator_1_eq), .clk(clock), .Q(d_immediate_op), .clr(reset));
  Register #(.width(1)) decoded_nzp_write_enable (
    .D(instcontrollogic_1_nzp_write), .en(comparator_1_eq), .clk(clock), .Q(d_nzp_write_enable_op),
    .clr(reset));
  Register #(.width(1)) decoded_reg_write_enable (
    .D(instcontrollogic_1_reg_write), .en(comparator_1_eq), .clk(clock), .Q(d_r_wr_enable_op), .clr(reset));
  Register #(.width(1)) decoded_mem_write_enable (
    .D(instcontrollogic_1_mem_write), .en(comparator_1_eq), .clk(clock), .Q(d_m_wr_enable_op), .clr(reset));
  InstControlLogic instcontrollogic_1 (
    .opCode(instruction[15:12]), .pc_mux(instcontrollogic_1_pc_mux),
    .reg_write(instcontrollogic_1_reg_write), .nzp_write(instcontrollogic_1_nzp_write),
    .alu_op_mux(instcontrollogic_1_alu_op_mux), .reg_input_mux(instcontrollogic_1_reg_input_mux),
    .alu_arithmetic_mux(instcontrollogic_1_alu_arithmetic_mux), .mem_read(instcontrollogic_1_mem_read),
    .mem_write(instcontrollogic_1_mem_write), .ret(instcontrollogic_1_ret));
  Register #(.width(1)) decoded_mem_read_enable (
    .D(instcontrollogic_1_mem_read), .en(comparator_1_eq), .clk(clock), .Q(d_m_rd_enable_op), .clr(reset));
endmodule

module InstControlLogic (
  input  [3:0] opCode,
  output pc_mux,
  output reg_write,
  output nzp_write,
  output alu_op_mux,
  output [1:0] reg_input_mux,
  output [1:0] alu_arithmetic_mux,
  output mem_read,
  output mem_write,
  output ret
);

  wire comparator_3_eq, comparator_4_eq, comparator_5_eq, comparator_6_eq;

  Comparator #(.mode("unsigned"), .width(4)) comparator_1 (.a(opCode), .b(4'b0001), .eq(pc_mux));  // open: gt, lt
  Comparator #(.mode("unsigned"), .width(4)) comparator_2 (.a(opCode), .b(4'b0010), .eq(alu_op_mux));  // open: gt, lt
  Comparator #(.mode("unsigned"), .width(4)) comparator_3 (
    .a(opCode), .b(4'b0011), .eq(comparator_3_eq));  // open: gt, lt
  Comparator #(.mode("unsigned"), .width(4)) comparator_4 (
    .a(opCode), .b(4'b0100), .eq(comparator_4_eq));  // open: gt, lt
  Comparator #(.mode("unsigned"), .width(4)) comparator_5 (
    .a(opCode), .b(4'b0101), .eq(comparator_5_eq));  // open: gt, lt
  Comparator #(.mode("unsigned"), .width(4)) comparator_6 (
    .a(opCode), .b(4'b0110), .eq(comparator_6_eq));  // open: gt, lt
  Comparator #(.mode("unsigned"), .width(4)) comparator_7 (.a(opCode), .b(4'b0111), .eq(mem_read));  // open: gt, lt
  Comparator #(.mode("unsigned"), .width(4)) comparator_8 (.a(opCode), .b(4'b1000), .eq(mem_write));  // open: gt, lt
  Comparator #(.mode("unsigned"), .width(4)) comparator_9 (
    .a(opCode), .b(4'b1001), .eq(reg_input_mux[1]));  // open: gt, lt
  Comparator #(.mode("unsigned"), .width(4)) comparator_10 (.a(opCode), .b(4'b1111), .eq(ret));  // open: gt, lt
  or or_1 (reg_write, comparator_3_eq, comparator_4_eq, comparator_5_eq, comparator_6_eq, mem_read, reg_input_mux[1]);
  or or_2 (alu_arithmetic_mux[0], comparator_4_eq, comparator_6_eq);
  or or_3 (alu_arithmetic_mux[1], comparator_5_eq, comparator_6_eq);

  assign nzp_write = alu_op_mux;
  assign reg_input_mux[0] = mem_read;
endmodule

module Fetcher (
  input  m_rd_ready,
  input  [7:0] current_pc,
  input  [2:0] core_state,
  input  [15:0] m_rd_data,
  input  clock,
  input  reset,
  output m_rd_valid_op,
  output [7:0] m_rd_address_op,
  output [2:0] fetch_st_op,
  output [15:0] inst_op
);

  wire and_1_out, and_2_out, and_3_out, and_4_out, and_5_out, comparator_1_eq, comparator_2_eq,
       comparator_3_eq, comparator_4_eq, comparator_5_eq, not_1_out, not_2_out, or_1_out, undriven;
  wire [2:0] multiplexer_4_out, multiplexer_6_out, multiplexer_7_out, multiplexer_8_out;
  wire [7:0] multiplexer_1_out, multiplexer_3_out;
  wire [15:0] multiplexer_2_out, multiplexer_5_out;

  Comparator #(.mode("unsigned"), .width(3)) comparator_1 (
    .a(3'b001), .b(fetch_st_op), .eq(comparator_1_eq));  // open: gt, lt
  Comparator #(.mode("unsigned"), .width(3)) comparator_2 (
    .a(3'b000), .b(fetch_st_op), .eq(comparator_2_eq));  // open: gt, lt
  Comparator #(.mode("unsigned"), .width(3)) comparator_3 (
    .a(3'b001), .b(core_state), .eq(comparator_3_eq));  // open: gt, lt
  Comparator #(.mode("unsigned"), .width(3)) comparator_4 (
    .a(3'b010), .b(fetch_st_op), .eq(comparator_4_eq));  // open: gt, lt
  Comparator #(.mode("unsigned"), .width(3)) comparator_5 (
    .a(3'b010), .b(core_state), .eq(comparator_5_eq));  // open: gt, lt
  not not_1 (not_1_out, and_1_out);
  and and_1 (and_1_out, m_rd_ready, comparator_1_eq);
  and and_2 (and_2_out, comparator_2_eq, comparator_3_eq);
  and and_3 (and_3_out, comparator_4_eq, comparator_5_eq);
  and and_4 (and_4_out, m_rd_valid_op, not_1_out);
  or or_1 (or_1_out, and_4_out, and_2_out);
  Multiplexer #(.width(8)) multiplexer_1 (
    .in0(m_rd_address_op), .in1(current_pc), .out(multiplexer_1_out), .sel(and_2_out));
  Multiplexer #(.width(16)) multiplexer_2 (.in0(inst_op), .in1(m_rd_data), .out(multiplexer_2_out), .sel(and_1_out));
  not not_2 (not_2_out, reset);
  Multiplexer #(.width(8)) multiplexer_3 (
    .in0(multiplexer_1_out), .in1({8{1'b0}}), .out(multiplexer_3_out), .sel(reset));
  Multiplexer #(.width(3)) multiplexer_4 (.in0(fetch_st_op), .in1(3'b001), .out(multiplexer_4_out), .sel(and_2_out));
  Multiplexer #(.width(16)) multiplexer_5 (
    .in0(multiplexer_2_out), .in1({16{1'b0}}), .out(multiplexer_5_out), .sel(reset));
  Register #(.width(1)) mem_read_valid (.D(and_5_out), .en(1'b1), .clk(clock), .Q(m_rd_valid_op));  // open: clr
  and and_5 (and_5_out, or_1_out, not_2_out);
  Register mem_read_address (.D(multiplexer_3_out), .en(1'b1), .clk(clock), .Q(m_rd_address_op));  // open: clr
  Multiplexer #(.width(3)) multiplexer_6 (
    .in0(multiplexer_4_out), .in1(3'b010), .out(multiplexer_6_out), .sel(and_1_out));
  Register #(.width(16)) instruction (.D(multiplexer_5_out), .en(1'b1), .clk(clock), .Q(inst_op));  // open: clr
  Multiplexer #(.width(3)) multiplexer_7 (
    .in0(multiplexer_6_out), .in1(3'b000), .out(multiplexer_7_out), .sel(and_3_out));
  Register #(.width(3)) fetcher_state (.D(multiplexer_8_out), .en(1'b1), .clk(clock), .Q(fetch_st_op), .clr(undriven));
  Multiplexer #(.width(3)) multiplexer_8 (.in0(multiplexer_7_out), .in1(3'b000), .out(multiplexer_8_out), .sel(reset));
endmodule

module LSU (
  input  [7:0] rs,
  input  [7:0] m_rd_data,
  input  enable,
  input  d_m_rd_enable,
  input  [7:0] rt,
  input  d_m_wr_enable,
  input  m_rd_ready,
  input  m_wr_ready,
  input  clock,
  input  [2:0] core_state,
  input  reset,
  output m_rd_valid_op,
  output [7:0] m_rd_addr_op,
  output [7:0] lsu_out_op,
  output m_wr_vld_op,
  output [7:0] m_wr_addr_op,
  output [7:0] m_wr_data_op,
  output [1:0] lsu_state_op
);

  wire LSUState1_is_idle, LSUState1_is_requesting, LSUState1_is_waiting;

  LSURead LSURead1 (
    .rs(rs), .mem_read_data(m_rd_data), .enable(enable), .decoded_mem_read_enable(d_m_rd_enable),
    .mem_read_ready(m_rd_ready), .is_idle(LSUState1_is_idle), .core_state(core_state),
    .is_waiting(LSUState1_is_waiting), .clock(clock), .reset(reset), .m_rd_valid_op(m_rd_valid_op),
    .m_rd_addr_op(m_rd_addr_op), .lsu_out_op(lsu_out_op));
  LSUState LSUState1 (
    .d_m_r_en(d_m_rd_enable), .d_m_w_en(d_m_wr_enable), .mem_read_ready(m_rd_ready),
    .mem_write_ready(m_wr_ready), .reset(reset), .enable(enable), .clock(clock), .core_state(core_state),
    .is_idle(LSUState1_is_idle), .lsu_state_op(lsu_state_op), .is_requesting(LSUState1_is_requesting),
    .is_waiting(LSUState1_is_waiting));  // open: is_done
  LSUWrite LSUWrite1 (
    .enable(enable), .is_requesting(LSUState1_is_requesting), .decoded_mem_write_enable(d_m_wr_enable),
    .is_waiting(LSUState1_is_waiting), .mem_write_ready(m_wr_ready), .rs(rs), .rt(rt), .clock(clock),
    .core_state(core_state), .reset(reset), .m_wr_va_op(m_wr_vld_op), .m_wr_addr_op(m_wr_addr_op),
    .m_wr_data_op(m_wr_data_op));
endmodule

module LSUState (
  input  d_m_r_en,
  input  d_m_w_en,
  input  mem_read_ready,
  input  mem_write_ready,
  input  reset,
  input  enable,
  input  clock,
  input  [2:0] core_state,
  output is_idle,
  output [1:0] lsu_state_op,
  output is_requesting,
  output is_waiting,
  output is_done
);

  wire and_1_out, and_2_out, and_3_out, and_4_out, and_5_out, comparator_1_eq, comparator_2_eq, or_1_out,
       or_2_out, or_3_out;
  wire [1:0] multiplexer_1_out, multiplexer_2_out, multiplexer_3_out, multiplexer_4_out, multiplexer_5_out;

  or or_1 (or_1_out, d_m_r_en, d_m_w_en);
  Comparator #(.mode("unsigned"), .width(3)) comparator_1 (
    .a(core_state), .b(3'b011), .eq(comparator_1_eq));  // open: gt, lt
  Comparator #(.mode("unsigned"), .width(3)) comparator_2 (
    .a(core_state), .b(3'b110), .eq(comparator_2_eq));  // open: gt, lt
  Comparator #(.mode("unsigned"), .width(2)) comparator_3 (.a(lsu_state_op), .b(2'b00), .eq(is_idle));  // open: gt, lt
  Comparator #(.mode("unsigned"), .width(2)) comparator_4 (
    .a(lsu_state_op), .b(2'b01), .eq(is_requesting));  // open: gt, lt
  Comparator #(.mode("unsigned"), .width(2)) comparator_5 (
    .a(lsu_state_op), .b(2'b10), .eq(is_waiting));  // open: gt, lt
  Comparator #(.mode("unsigned"), .width(2)) comparator_6 (.a(lsu_state_op), .b(2'b11), .eq(is_done));  // open: gt, lt
  and and_1 (and_1_out, is_idle, comparator_1_eq, or_1_out);
  and and_2 (and_2_out, is_waiting, d_m_r_en, mem_read_ready);
  and and_3 (and_3_out, is_waiting, d_m_w_en, mem_write_ready);
  Multiplexer #(.width(2)) multiplexer_1 (.in0(lsu_state_op), .in1(2'b01), .out(multiplexer_1_out), .sel(and_1_out));
  Multiplexer #(.width(2)) multiplexer_2 (
    .in0(multiplexer_1_out), .in1(2'b10), .out(multiplexer_2_out), .sel(and_4_out));
  and and_4 (and_4_out, or_1_out, is_requesting);
  or or_2 (or_2_out, and_2_out, and_3_out);
  Multiplexer #(.width(2)) multiplexer_3 (
    .in0(multiplexer_2_out), .in1(2'b11), .out(multiplexer_3_out), .sel(or_2_out));
  Multiplexer #(.width(2)) multiplexer_4 (
    .in0(multiplexer_3_out), .in1(2'b00), .out(multiplexer_4_out), .sel(and_5_out));
  and and_5 (and_5_out, is_done, comparator_2_eq, or_1_out);
  Multiplexer #(.width(2)) multiplexer_5 (.in0(multiplexer_4_out), .in1(2'b00), .out(multiplexer_5_out), .sel(reset));
  or or_3 (or_3_out, reset, enable);
  Register #(.width(2)) lsu_state (.D(multiplexer_5_out), .en(or_3_out), .clk(clock), .Q(lsu_state_op));  // open: clr
endmodule

module LSURead (
  input  [7:0] rs,
  input  [7:0] mem_read_data,
  input  enable,
  input  decoded_mem_read_enable,
  input  mem_read_ready,
  input  is_idle,
  input  [2:0] core_state,
  input  is_waiting,
  input  clock,
  input  reset,
  output m_rd_valid_op,
  output [7:0] m_rd_addr_op,
  output [7:0] lsu_out_op
);

  wire and_1_out, and_2_out, comparator_1_eq, multiplexer_1_out, multiplexer_2_out, multiplexer_3_out,
       or_1_out;
  wire [7:0] multiplexer_4_out, multiplexer_5_out, multiplexer_6_out, multiplexer_7_out;

  Multiplexer multiplexer_1 (.in0(m_rd_valid_op), .in1(1'b0), .out(multiplexer_1_out), .sel(and_1_out));
  and and_1 (and_1_out, is_waiting, decoded_mem_read_enable, mem_read_ready);
  Comparator #(.mode("unsigned"), .width(3)) comparator_1 (
    .a(core_state), .b(3'b011), .eq(comparator_1_eq));  // open: gt, lt
  and and_2 (and_2_out, is_idle, comparator_1_eq, decoded_mem_read_enable);
  Multiplexer multiplexer_2 (.in0(multiplexer_1_out), .in1(1'b1), .out(multiplexer_2_out), .sel(and_2_out));
  Multiplexer multiplexer_3 (.in0(multiplexer_2_out), .in1(1'b0), .out(multiplexer_3_out), .sel(reset));
  Register #(.width(1)) mem_read_valid (
    .D(multiplexer_3_out), .en(or_1_out), .clk(clock), .Q(m_rd_valid_op));  // open: clr
  or or_1 (or_1_out, enable, reset);
  Multiplexer #(.width(8)) multiplexer_4 (.in0(m_rd_addr_op), .in1(rs), .out(multiplexer_4_out), .sel(and_2_out));
  Multiplexer #(.width(8)) multiplexer_5 (
    .in0(lsu_out_op), .in1(mem_read_data), .out(multiplexer_5_out), .sel(and_1_out));
  Register mem_read_address (.D(multiplexer_6_out), .en(or_1_out), .clk(clock), .Q(m_rd_addr_op));  // open: clr
  Multiplexer #(.width(8)) multiplexer_6 (
    .in0(multiplexer_4_out), .in1({8{1'b0}}), .out(multiplexer_6_out), .sel(reset));
  Multiplexer #(.width(8)) multiplexer_7 (
    .in0(multiplexer_5_out), .in1({8{1'b0}}), .out(multiplexer_7_out), .sel(reset));
  Register lsu_out (.D(multiplexer_7_out), .en(or_1_out), .clk(clock), .Q(lsu_out_op));  // open: clr
endmodule

module LSUWrite (
  input  enable,
  input  is_requesting,
  input  decoded_mem_write_enable,
  input  is_waiting,
  input  mem_write_ready,
  input  [7:0] rs,
  input  [7:0] rt,
  input  clock,
  input  [2:0] core_state,
  input  reset,
  output m_wr_va_op,
  output [7:0] m_wr_addr_op,
  output [7:0] m_wr_data_op
);

  wire and_1_out, and_2_out, multiplexer_1_out, multiplexer_4_out, multiplexer_5_out;
  wire [7:0] multiplexer_2_out, multiplexer_3_out, multiplexer_6_out, multiplexer_7_out;

  and and_1 (and_1_out, enable, is_requesting, decoded_mem_write_enable);
  and and_2 (and_2_out, enable, decoded_mem_write_enable, is_waiting, mem_write_ready);
  Multiplexer multiplexer_1 (.in0(m_wr_va_op), .in1(1'b1), .out(multiplexer_1_out), .sel(and_1_out));
  Multiplexer #(.width(8)) multiplexer_2 (.in0(m_wr_addr_op), .in1(rs), .out(multiplexer_2_out), .sel(and_1_out));
  Multiplexer #(.width(8)) multiplexer_3 (.in0(m_wr_data_op), .in1(rt), .out(multiplexer_3_out), .sel(and_1_out));
  Multiplexer multiplexer_4 (.in0(multiplexer_1_out), .in1(1'b0), .out(multiplexer_4_out), .sel(and_2_out));
  Multiplexer multiplexer_5 (.in0(multiplexer_4_out), .in1(1'b0), .out(multiplexer_5_out), .sel(reset));
  Register mem_write_address (.D(multiplexer_6_out), .en(1'b1), .clk(clock), .Q(m_wr_addr_op));  // open: clr
  Multiplexer #(.width(8)) multiplexer_6 (
    .in0(multiplexer_2_out), .in1({8{1'b0}}), .out(multiplexer_6_out), .sel(reset));
  Register mem_write_data (.D(multiplexer_7_out), .en(1'b1), .clk(clock), .Q(m_wr_data_op));  // open: clr
  Multiplexer #(.width(8)) multiplexer_7 (
    .in0(multiplexer_3_out), .in1({8{1'b0}}), .out(multiplexer_7_out), .sel(reset));
  Register #(.width(1)) mem_write_valid (.D(multiplexer_5_out), .en(1'b1), .clk(clock), .Q(m_wr_va_op));  // open: clr
endmodule

module SchedulerState (
  input  decoded_ret,
  input  [1:0] lsu_state_0,
  input  [1:0] lsu_state_1,
  input  [1:0] lsu_state_2,
  input  [1:0] lsu_state_3,
  input  [2:0] fetc_st,
  input  [7:0] next_pc_3,
  input  start,
  input  clock,
  input  reset,
  output done_op,
  output [2:0] core_state_op,
  output [7:0] curr_pc_op
);

  wire and_1_out, and_2_out, and_3_out, and_4_out, and_5_out, AnyLSUWaiting1_any_lsu_waiting_op,
       comparator_1_eq, comparator_2_eq, comparator_3_eq, comparator_4_eq, comparator_5_eq, comparator_6_eq,
       comparator_7_eq, comparator_8_eq, multiplexer_9_out, multiplexer_11_out, not_1_out, not_2_out;
  wire [2:0] multiplexer_1_out, multiplexer_2_out, multiplexer_3_out, multiplexer_4_out, multiplexer_5_out,
       multiplexer_6_out, multiplexer_7_out, multiplexer_8_out, multiplexer_10_out;
  wire [7:0] multiplexer_12_out, multiplexer_13_out;

  not not_1 (not_1_out, decoded_ret);
  Comparator #(.mode("unsigned"), .width(3)) comparator_1 (
    .a(3'b110), .b(core_state_op), .eq(comparator_1_eq));  // open: gt, lt
  Multiplexer #(.width(3)) multiplexer_1 (.in0(core_state_op), .in1(3'b001), .out(multiplexer_1_out), .sel(and_1_out));
  and and_1 (and_1_out, not_1_out, comparator_1_eq);
  and and_2 (and_2_out, decoded_ret, comparator_1_eq);
  Multiplexer #(.width(3)) multiplexer_2 (
    .in0(multiplexer_1_out), .in1(3'b111), .out(multiplexer_2_out), .sel(and_2_out));
  Comparator #(.mode("unsigned"), .width(3)) comparator_2 (
    .a(3'b101), .b(core_state_op), .eq(comparator_2_eq));  // open: gt, lt
  AnyLSUWaiting AnyLSUWaiting1 (
    .lsu_state_0(lsu_state_0), .lsu_state_1(lsu_state_1), .lsu_state_2(lsu_state_2),
    .lsu_state_3(lsu_state_3), .any_lsu_waiting_op(AnyLSUWaiting1_any_lsu_waiting_op));
  Multiplexer #(.width(3)) multiplexer_3 (
    .in0(multiplexer_2_out), .in1(3'b110), .out(multiplexer_3_out), .sel(comparator_2_eq));
  Comparator #(.mode("unsigned"), .width(3)) comparator_3 (
    .a(3'b100), .b(core_state_op), .eq(comparator_3_eq));  // open: gt, lt
  not not_2 (not_2_out, AnyLSUWaiting1_any_lsu_waiting_op);
  Multiplexer #(.width(3)) multiplexer_4 (
    .in0(multiplexer_3_out), .in1(3'b101), .out(multiplexer_4_out), .sel(and_3_out));
  and and_3 (and_3_out, comparator_3_eq, not_2_out);
  Comparator #(.mode("unsigned"), .width(3)) comparator_4 (
    .a(3'b011), .b(core_state_op), .eq(comparator_4_eq));  // open: gt, lt
  Multiplexer #(.width(3)) multiplexer_5 (
    .in0(multiplexer_4_out), .in1(3'b100), .out(multiplexer_5_out), .sel(comparator_4_eq));
  Comparator #(.mode("unsigned"), .width(3)) comparator_5 (
    .a(3'b010), .b(core_state_op), .eq(comparator_5_eq));  // open: gt, lt
  Comparator #(.mode("unsigned"), .width(3)) comparator_6 (
    .a(core_state_op), .b(3'b001), .eq(comparator_6_eq));  // open: gt, lt
  Comparator #(.mode("unsigned"), .width(3)) comparator_7 (
    .a(fetc_st), .b(3'b010), .eq(comparator_7_eq));  // open: gt, lt
  Multiplexer #(.width(3)) multiplexer_6 (
    .in0(multiplexer_5_out), .in1(3'b011), .out(multiplexer_6_out), .sel(comparator_5_eq));
  and and_4 (and_4_out, comparator_6_eq, comparator_7_eq);
  Comparator #(.mode("unsigned"), .width(3)) comparator_8 (
    .a(core_state_op), .b(3'b000), .eq(comparator_8_eq));  // open: gt, lt
  Multiplexer #(.width(3)) multiplexer_7 (
    .in0(multiplexer_6_out), .in1(3'b010), .out(multiplexer_7_out), .sel(and_4_out));
  and and_5 (and_5_out, comparator_8_eq, start);
  Multiplexer #(.width(3)) multiplexer_8 (
    .in0(multiplexer_7_out), .in1(3'b001), .out(multiplexer_8_out), .sel(and_5_out));
  Multiplexer multiplexer_9 (.in0(done_op), .in1(1'b1), .out(multiplexer_9_out), .sel(and_2_out));
  Register #(.width(3)) core_state (.D(multiplexer_10_out), .en(1'b1), .clk(clock), .Q(core_state_op));  // open: clr
  Multiplexer #(.width(3)) multiplexer_10 (
    .in0(multiplexer_8_out), .in1(3'b000), .out(multiplexer_10_out), .sel(reset));
  Register #(.width(1)) done (.D(multiplexer_11_out), .en(1'b1), .clk(clock), .Q(done_op));  // open: clr
  Multiplexer multiplexer_11 (.in0(multiplexer_9_out), .in1(1'b0), .out(multiplexer_11_out), .sel(reset));
  Multiplexer #(.width(8)) multiplexer_12 (
    .in0(curr_pc_op), .in1(next_pc_3), .out(multiplexer_12_out), .sel(and_1_out));
  Register current_pc (.D(multiplexer_13_out), .en(1'b1), .clk(clock), .Q(curr_pc_op));  // open: clr
  Multiplexer #(.width(8)) multiplexer_13 (
    .in0(multiplexer_12_out), .in1({8{1'b0}}), .out(multiplexer_13_out), .sel(reset));
endmodule

module AnyLSUWaiting (
  input  [1:0] lsu_state_0,
  input  [1:0] lsu_state_1,
  input  [1:0] lsu_state_2,
  input  [1:0] lsu_state_3,
  output any_lsu_waiting_op
);

  wire comparator_1_eq, comparator_2_eq, comparator_3_eq, comparator_4_eq, comparator_5_eq, comparator_6_eq,
       comparator_7_eq, comparator_8_eq, or_1_out, or_2_out, or_3_out, or_4_out;

  Comparator #(.mode("unsigned"), .width(2)) comparator_1 (
    .a(2'b01), .b(lsu_state_0), .eq(comparator_1_eq));  // open: gt, lt
  Comparator #(.mode("unsigned"), .width(2)) comparator_2 (
    .a(lsu_state_0), .b(2'b10), .eq(comparator_2_eq));  // open: gt, lt
  Comparator #(.mode("unsigned"), .width(2)) comparator_3 (
    .a(2'b01), .b(lsu_state_1), .eq(comparator_3_eq));  // open: gt, lt
  Comparator #(.mode("unsigned"), .width(2)) comparator_4 (
    .a(lsu_state_1), .b(2'b10), .eq(comparator_4_eq));  // open: gt, lt
  Comparator #(.mode("unsigned"), .width(2)) comparator_5 (
    .a(2'b01), .b(lsu_state_2), .eq(comparator_5_eq));  // open: gt, lt
  Comparator #(.mode("unsigned"), .width(2)) comparator_6 (
    .a(lsu_state_2), .b(2'b10), .eq(comparator_6_eq));  // open: gt, lt
  Comparator #(.mode("unsigned"), .width(2)) comparator_7 (
    .a(2'b01), .b(lsu_state_3), .eq(comparator_7_eq));  // open: gt, lt
  Comparator #(.mode("unsigned"), .width(2)) comparator_8 (
    .a(lsu_state_3), .b(2'b10), .eq(comparator_8_eq));  // open: gt, lt
  or or_1 (or_1_out, comparator_1_eq, comparator_2_eq);
  or or_2 (or_2_out, comparator_3_eq, comparator_4_eq);
  or or_3 (or_3_out, comparator_5_eq, comparator_6_eq);
  or or_4 (or_4_out, comparator_7_eq, comparator_8_eq);
  or or_5 (any_lsu_waiting_op, or_1_out, or_2_out, or_3_out, or_4_out);
endmodule

module Core (
  input  start,
  input  p_m_rd_ready,
  input  [15:0] p_m_rd_data,
  input  clock,
  input  reset,
  input  [7:0] blk_id_in,
  input  [7:0] d2_m_rd_data,
  input  [7:0] d3_m_rd_data,
  input  [7:0] d1_m_rd_data,
  input  [7:0] d0_m_rd_data,
  input  [7:0] thread_count,
  input  d0_m_rd_ready,
  input  d1_m_rd_ready,
  input  d2_m_rd_ready,
  input  d3_m_rd_ready,
  input  d0_m_wr_ready,
  input  d1_m_wr_ready,
  input  d2_m_wr_ready,
  input  d3_m_wr_ready,
  output done_op,
  output p_m_rd_valid,
  output [7:0] p_m_rd_addr,
  output d3_m_wr_valid,
  output d1_m_wr_valid,
  output d2_m_wr_valid,
  output d0_m_wr_valid,
  output [7:0] d3_m_wr_addr,
  output [7:0] d1_m_wr_addr,
  output [7:0] d2_m_wr_addr,
  output [7:0] d0_m_wr_addr,
  output [7:0] d3_m_wr_data,
  output [7:0] d0_m_wr_data,
  output [7:0] d1_m_wr_data,
  output [7:0] d2_m_wr_data,
  output d3_m_rd_valid,
  output d0_m_rd_valid,
  output d2_m_rd_valid,
  output d1_m_rd_valid,
  output [7:0] d3_m_rd_addr,
  output [7:0] d0_m_rd_addr,
  output [7:0] d2_m_rd_addr,
  output [7:0] d1_m_rd_addr
);

  wire comparator_1_lt, comparator_2_lt, comparator_3_lt, comparator_4_lt, instdecode_1_d_alu_output_mux_op,
       instdecode_1_d_m_rd_enable_op, instdecode_1_d_m_wr_enable_op, instdecode_1_d_nzp_write_enable_op,
       instdecode_1_d_pc_mux_op, instdecode_1_d_r_wr_enable_op, instdecode_1_d_ret_op;
  wire [1:0] instdecode_1_d_alu_arithmetic_mux_op, instdecode_1_d_r_inp_mux_op, thread_1_lsu_st_op,
       thread_2_lsu_st_op, thread_3_lsu_st_op, thread_4_lsu_st_op;
  wire [2:0] fetcher_1_fetch_st_op, instdecode_1_d_nzp_op, schedulerstate_1_core_state_op;
  wire [3:0] instdecode_1_d_rd_address_op, instdecode_1_d_rs_address_op, instdecode_1_d_rt_address_op;
  wire [7:0] instdecode_1_d_immediate_op, schedulerstate_1_curr_pc_op, thread_4_nxt_pc_op;
  wire [15:0] fetcher_1_inst_op;

  Comparator comparator_1 (.a({8{1'b0}}), .b(thread_count), .lt(comparator_1_lt));  // open: gt, eq
  Fetcher fetcher_1 (
    .m_rd_ready(p_m_rd_ready), .current_pc(schedulerstate_1_curr_pc_op),
    .core_state(schedulerstate_1_core_state_op), .m_rd_data(p_m_rd_data), .clock(clock), .reset(reset),
    .m_rd_valid_op(p_m_rd_valid), .m_rd_address_op(p_m_rd_addr), .fetch_st_op(fetcher_1_fetch_st_op),
    .inst_op(fetcher_1_inst_op));
  Thread thread_1 (
    .blk_dim_in(8'h4), .d_rt_addr(instdecode_1_d_rt_address_op), .d_rs_addr(instdecode_1_d_rs_address_op),
    .thrd_id_in({8{1'b0}}), .d_imm(instdecode_1_d_immediate_op), .d_nzp(instdecode_1_d_nzp_op),
    .blk_id_in(blk_id_in), .curr_pc(schedulerstate_1_curr_pc_op), .d_r_wr_en(instdecode_1_d_r_wr_enable_op),
    .d_r_in_mux(instdecode_1_d_r_inp_mux_op), .d_m_rd_data(d0_m_rd_data),
    .d_m_rd_en(instdecode_1_d_m_rd_enable_op), .d_m_wr_en(instdecode_1_d_m_wr_enable_op),
    .d_m_rd_ready(d0_m_rd_ready), .d_m_wr_ready(d0_m_wr_ready), .d_rd_addr(instdecode_1_d_rd_address_op),
    .d_nzp_wr_en(instdecode_1_d_nzp_write_enable_op), .clock(clock), .d_pc_mux(instdecode_1_d_pc_mux_op),
    .reset(reset), .core_state(schedulerstate_1_core_state_op),
    .d_alu_arth_mux(instdecode_1_d_alu_arithmetic_mux_op), .d_alu_op_mux(instdecode_1_d_alu_output_mux_op),
    .enable(comparator_1_lt), .d_m_wr_valid(d0_m_wr_valid), .d_m_wr_addr(d0_m_wr_addr),
    .d_m_wr_data(d0_m_wr_data), .lsu_st_op(thread_1_lsu_st_op), .d_m_rd_valid(d0_m_rd_valid),
    .d_m_rd_addr(d0_m_rd_addr));  // open: nxt_pc_op
  InstDecode instdecode_1 (
    .instruction(fetcher_1_inst_op), .clock(clock), .reset(reset),
    .core_state(schedulerstate_1_core_state_op), .d_rd_address_op(instdecode_1_d_rd_address_op),
    .d_rs_address_op(instdecode_1_d_rs_address_op), .d_rt_address_op(instdecode_1_d_rt_address_op),
    .d_nzp_op(instdecode_1_d_nzp_op), .d_immediate_op(instdecode_1_d_immediate_op),
    .d_r_wr_enable_op(instdecode_1_d_r_wr_enable_op), .d_m_rd_enable_op(instdecode_1_d_m_rd_enable_op),
    .d_m_wr_enable_op(instdecode_1_d_m_wr_enable_op),
    .d_nzp_write_enable_op(instdecode_1_d_nzp_write_enable_op), .d_r_inp_mux_op(instdecode_1_d_r_inp_mux_op),
    .d_alu_arithmetic_mux_op(instdecode_1_d_alu_arithmetic_mux_op),
    .d_alu_output_mux_op(instdecode_1_d_alu_output_mux_op), .d_pc_mux_op(instdecode_1_d_pc_mux_op),
    .d_ret_op(instdecode_1_d_ret_op));
  Comparator comparator_2 (.a(8'h1), .b(thread_count), .lt(comparator_2_lt));  // open: gt, eq
  SchedulerState schedulerstate_1 (
    .decoded_ret(instdecode_1_d_ret_op), .lsu_state_0(thread_1_lsu_st_op), .lsu_state_1(thread_2_lsu_st_op),
    .lsu_state_2(thread_3_lsu_st_op), .lsu_state_3(thread_4_lsu_st_op), .fetc_st(fetcher_1_fetch_st_op),
    .next_pc_3(thread_4_nxt_pc_op), .start(start), .clock(clock), .reset(reset), .done_op(done_op),
    .core_state_op(schedulerstate_1_core_state_op), .curr_pc_op(schedulerstate_1_curr_pc_op));
  Thread thread_2 (
    .blk_dim_in(8'h4), .d_rt_addr(instdecode_1_d_rt_address_op), .d_rs_addr(instdecode_1_d_rs_address_op),
    .thrd_id_in(8'h1), .d_imm(instdecode_1_d_immediate_op), .d_nzp(instdecode_1_d_nzp_op),
    .blk_id_in(blk_id_in), .curr_pc(schedulerstate_1_curr_pc_op), .d_r_wr_en(instdecode_1_d_r_wr_enable_op),
    .d_r_in_mux(instdecode_1_d_r_inp_mux_op), .d_m_rd_data(d1_m_rd_data),
    .d_m_rd_en(instdecode_1_d_m_rd_enable_op), .d_m_wr_en(instdecode_1_d_m_wr_enable_op),
    .d_m_rd_ready(d1_m_rd_ready), .d_m_wr_ready(d1_m_wr_ready), .d_rd_addr(instdecode_1_d_rd_address_op),
    .d_nzp_wr_en(instdecode_1_d_nzp_write_enable_op), .clock(clock), .d_pc_mux(instdecode_1_d_pc_mux_op),
    .reset(reset), .core_state(schedulerstate_1_core_state_op),
    .d_alu_arth_mux(instdecode_1_d_alu_arithmetic_mux_op), .d_alu_op_mux(instdecode_1_d_alu_output_mux_op),
    .enable(comparator_2_lt), .d_m_wr_valid(d1_m_wr_valid), .d_m_wr_addr(d1_m_wr_addr),
    .d_m_wr_data(d1_m_wr_data), .lsu_st_op(thread_2_lsu_st_op), .d_m_rd_valid(d1_m_rd_valid),
    .d_m_rd_addr(d1_m_rd_addr));  // open: nxt_pc_op
  Comparator comparator_3 (.a(8'h2), .b(thread_count), .lt(comparator_3_lt));  // open: gt, eq
  Thread thread_3 (
    .blk_dim_in(8'h4), .d_rt_addr(instdecode_1_d_rt_address_op), .d_rs_addr(instdecode_1_d_rs_address_op),
    .thrd_id_in(8'h2), .d_imm(instdecode_1_d_immediate_op), .d_nzp(instdecode_1_d_nzp_op),
    .blk_id_in(blk_id_in), .curr_pc(schedulerstate_1_curr_pc_op), .d_r_wr_en(instdecode_1_d_r_wr_enable_op),
    .d_r_in_mux(instdecode_1_d_r_inp_mux_op), .d_m_rd_data(d2_m_rd_data),
    .d_m_rd_en(instdecode_1_d_m_rd_enable_op), .d_m_wr_en(instdecode_1_d_m_wr_enable_op),
    .d_m_rd_ready(d2_m_rd_ready), .d_m_wr_ready(d2_m_wr_ready), .d_rd_addr(instdecode_1_d_rd_address_op),
    .d_nzp_wr_en(instdecode_1_d_nzp_write_enable_op), .clock(clock), .d_pc_mux(instdecode_1_d_pc_mux_op),
    .reset(reset), .core_state(schedulerstate_1_core_state_op),
    .d_alu_arth_mux(instdecode_1_d_alu_arithmetic_mux_op), .d_alu_op_mux(instdecode_1_d_alu_output_mux_op),
    .enable(comparator_3_lt), .d_m_wr_valid(d2_m_wr_valid), .d_m_wr_addr(d2_m_wr_addr),
    .d_m_wr_data(d2_m_wr_data), .lsu_st_op(thread_3_lsu_st_op), .d_m_rd_valid(d2_m_rd_valid),
    .d_m_rd_addr(d2_m_rd_addr));  // open: nxt_pc_op
  Comparator comparator_4 (.a(8'h3), .b(thread_count), .lt(comparator_4_lt));  // open: gt, eq
  Thread thread_4 (
    .blk_dim_in(8'h4), .d_rt_addr(instdecode_1_d_rt_address_op), .d_rs_addr(instdecode_1_d_rs_address_op),
    .thrd_id_in(8'h3), .d_imm(instdecode_1_d_immediate_op), .d_nzp(instdecode_1_d_nzp_op),
    .blk_id_in(blk_id_in), .curr_pc(schedulerstate_1_curr_pc_op), .d_r_wr_en(instdecode_1_d_r_wr_enable_op),
    .d_r_in_mux(instdecode_1_d_r_inp_mux_op), .d_m_rd_data(d3_m_rd_data),
    .d_m_rd_en(instdecode_1_d_m_rd_enable_op), .d_m_wr_en(instdecode_1_d_m_wr_enable_op),
    .d_m_rd_ready(d3_m_rd_ready), .d_m_wr_ready(d3_m_wr_ready), .d_rd_addr(instdecode_1_d_rd_address_op),
    .d_nzp_wr_en(instdecode_1_d_nzp_write_enable_op), .clock(clock), .d_pc_mux(instdecode_1_d_pc_mux_op),
    .reset(reset), .core_state(schedulerstate_1_core_state_op),
    .d_alu_arth_mux(instdecode_1_d_alu_arithmetic_mux_op), .d_alu_op_mux(instdecode_1_d_alu_output_mux_op),
    .enable(comparator_4_lt), .d_m_wr_valid(d3_m_wr_valid), .d_m_wr_addr(d3_m_wr_addr),
    .nxt_pc_op(thread_4_nxt_pc_op), .d_m_wr_data(d3_m_wr_data), .lsu_st_op(thread_4_lsu_st_op),
    .d_m_rd_valid(d3_m_rd_valid), .d_m_rd_addr(d3_m_rd_addr));
endmodule

module Thread (
  input  [7:0] blk_dim_in,
  input  [3:0] d_rt_addr,
  input  [3:0] d_rs_addr,
  input  [7:0] thrd_id_in,
  input  [7:0] d_imm,
  input  [2:0] d_nzp,
  input  [7:0] blk_id_in,
  input  [7:0] curr_pc,
  input  d_r_wr_en,
  input  [1:0] d_r_in_mux,
  input  [7:0] d_m_rd_data,
  input  d_m_rd_en,
  input  d_m_wr_en,
  input  d_m_rd_ready,
  input  d_m_wr_ready,
  input  [3:0] d_rd_addr,
  input  d_nzp_wr_en,
  input  clock,
  input  d_pc_mux,
  input  reset,
  input  [2:0] core_state,
  input  [1:0] d_alu_arth_mux,
  input  d_alu_op_mux,
  input  enable,
  output d_m_wr_valid,
  output [7:0] d_m_wr_addr,
  output [7:0] nxt_pc_op,
  output [7:0] d_m_wr_data,
  output [1:0] lsu_st_op,
  output d_m_rd_valid,
  output [7:0] d_m_rd_addr
);

  wire [7:0] alu_1_alu_out, lsu_1_lsu_out_op, registers_1_rs_op, registers_1_rt_op;

  LSU lsu_1 (
    .rs(registers_1_rs_op), .m_rd_data(d_m_rd_data), .enable(enable), .d_m_rd_enable(d_m_rd_en),
    .rt(registers_1_rt_op), .d_m_wr_enable(d_m_wr_en), .m_rd_ready(d_m_rd_ready), .m_wr_ready(d_m_wr_ready),
    .clock(clock), .core_state(core_state), .reset(reset), .m_rd_valid_op(d_m_rd_valid),
    .m_rd_addr_op(d_m_rd_addr), .lsu_out_op(lsu_1_lsu_out_op), .m_wr_vld_op(d_m_wr_valid),
    .m_wr_addr_op(d_m_wr_addr), .m_wr_data_op(d_m_wr_data), .lsu_state_op(lsu_st_op));
  Registers registers_1 (
    .d_rt_address(d_rt_addr), .d_rs_address(d_rs_addr), .reset(reset), .blockDim(blk_dim_in),
    .threadIdx(thrd_id_in), .alu_out(alu_1_alu_out), .lsu_out(lsu_1_lsu_out_op), .blockId(blk_id_in),
    .d_immediate(d_imm), .d_r_in_mux(d_r_in_mux), .clock(clock), .enable(enable), .core_state(core_state),
    .d_r_wr_enable(d_r_wr_en), .d_rd_address(d_rd_addr), .rt_op(registers_1_rt_op), .rs_op(registers_1_rs_op));
  ALU alu_1 (
    .core_state(core_state), .enable(enable), .rs(registers_1_rs_op), .reset(reset), .rt(registers_1_rt_op),
    .d_alu_output_mux(d_alu_op_mux), .clock(clock), .d_alu_arithmetic_mux(d_alu_arth_mux),
    .alu_out(alu_1_alu_out));
  PC pc_1 (
    .enable(enable), .current_pc(curr_pc), .d_immediate(d_imm), .d_nzp(d_nzp), .alu_out(alu_1_alu_out),
    .d_pc_mux(d_pc_mux), .clock(clock), .reset(reset), .core_state(core_state),
    .d_nzp_wr_enable(d_nzp_wr_en), .next_pc_op(nxt_pc_op));
endmodule

module Dispatcher (
  input  [1:0] core_done,
  input  [7:0] thread_count,
  input  start,
  input  clock,
  input  reset,
  output [1:0] core_start_op,
  output [1:0] core_reset_op,
  output [7:0] c_b_id_0_op,
  output [7:0] c_b_id_1_op,
  output [2:0] c_t_cnt_0_op,
  output [2:0] c_t_cnt_1_op,
  output done_op
);

  wire and_1_out, and_2_out, and_3_out, comparator_1_eq, comparator_2_eq, comparator_3_lt, comparator_4_lt,
       comparator_5_eq, comparator_6_eq, multiplexer_15_out, multiplexer_21_out, not_1_out, not_2_out,
       not_3_out, or_1_out, or_2_out;
  wire [1:0] adder_4_out, and_4_out, and_6_out, bit_extender_4_out, bit_extender_5_out, multiplexer_9_out,
       multiplexer_10_out, multiplexer_16_out;
  wire [2:0] bit_extender_1_out, multiplexer_1_out, multiplexer_6_out, multiplexer_7_out, multiplexer_13_out,
       multiplexer_14_out, multiplexer_19_out, multiplexer_20_out, subtractor_1_out;
  wire [4:0] subtractor_1_out_2;
  wire [7:0] adder_1_out, adder_2_out, adder_3_out, adder_5_out, bit_extender_2_out, bit_extender_3_out,
       bit_extender_6_out, blocks_dispatched_q, blocks_done_q, multiplexer_2_out, multiplexer_3_out,
       multiplexer_4_out, multiplexer_5_out, multiplexer_8_out, multiplexer_11_out, multiplexer_12_out,
       multiplexer_17_out, multiplexer_18_out, shifter_1_out, subtractor_2_out;

  Comparator #(.mode("unsigned"), .width(2)) comparator_1 (
    .a(thread_count[1:0]), .b(2'b00), .eq(comparator_1_eq));  // open: gt, lt
  assign bit_extender_1_out = {{1{1'b0}}, thread_count[1:0]};  // Bit_Extender bit_extender_1
  not not_1 (not_1_out, comparator_2_eq);
  Comparator #(.mode("unsigned"), .width(2)) comparator_2 (
    .a(thread_count[1:0]), .b(2'b00), .eq(comparator_2_eq));  // open: gt, lt
  assign bit_extender_2_out = {{2{1'b0}}, thread_count[7:2]};  // Bit_Extender bit_extender_2
  Multiplexer #(.width(3)) multiplexer_1 (
    .in0(bit_extender_1_out), .in1(3'b100), .out(multiplexer_1_out), .sel(comparator_1_eq));
  assign bit_extender_3_out = {{7{1'b0}}, not_1_out};  // Bit_Extender bit_extender_3
  Adder adder_1 (.a(bit_extender_3_out), .b(bit_extender_2_out), .out(adder_1_out));  // open: cin, cout
  Multiplexer #(.width(8)) multiplexer_2 (
    .in0(multiplexer_8_out), .in1({8{1'b0}}), .out(multiplexer_2_out), .sel(reset));
  Multiplexer #(.width(8)) multiplexer_3 (.in0(blocks_done_q), .in1(adder_5_out), .out(multiplexer_3_out), .sel(start));
  Multiplexer #(.width(8)) multiplexer_4 (
    .in0(multiplexer_3_out), .in1({8{1'b0}}), .out(multiplexer_4_out), .sel(reset));
  Shifter shifter_1 (.in(blocks_dispatched_q), .\dist (3'b010), .out(shifter_1_out));
  Adder adder_2 (.a(blocks_dispatched_q), .b(8'h1), .out(adder_2_out));  // open: cin, cout
  Register blocks_dispatched (.D(multiplexer_2_out), .en(1'b1), .clk(clock), .Q(blocks_dispatched_q));  // open: clr
  Register blocks_done (.D(multiplexer_4_out), .en(1'b1), .clk(clock), .Q(blocks_done_q));  // open: clr
  Subtractor subtractor_1 (
    .a(thread_count), .b(shifter_1_out), .out({subtractor_1_out_2, subtractor_1_out}));  // open: bin, bout
  Subtractor subtractor_2 (.a(adder_1_out), .b(8'h1), .out(subtractor_2_out));  // open: bin, bout
  Comparator #(.mode("unsigned")) comparator_3 (
    .a(multiplexer_5_out), .b(adder_1_out), .lt(comparator_3_lt));  // open: gt, eq
  Comparator #(.mode("unsigned")) comparator_4 (
    .a(blocks_dispatched_q), .b(adder_1_out), .lt(comparator_4_lt));  // open: gt, eq
  Comparator #(.mode("unsigned")) comparator_5 (
    .a(blocks_dispatched_q), .b(subtractor_2_out), .eq(comparator_5_eq));  // open: gt, lt
  and and_1 (and_1_out, comparator_3_lt, core_reset_op[1], start);
  and and_2 (and_2_out, start, core_reset_op[0], comparator_4_lt);
  Comparator comparator_6 (.a(blocks_done_q), .b(adder_1_out), .eq(comparator_6_eq));  // open: gt, lt
  Multiplexer #(.width(8)) multiplexer_5 (
    .in0(blocks_dispatched_q), .in1(adder_2_out), .out(multiplexer_5_out), .sel(and_2_out));
  and and_3 (and_3_out, comparator_6_eq, start);
  Adder adder_3 (.a(8'h1), .b(multiplexer_5_out), .out(adder_3_out), .cin(1'b0));  // open: cout
  Multiplexer #(.width(3)) multiplexer_6 (
    .in0(3'b100), .in1(subtractor_1_out), .out(multiplexer_6_out), .sel(comparator_5_eq));
  Multiplexer #(.width(3)) multiplexer_7 (
    .in0(3'b100), .in1(subtractor_1_out), .out(multiplexer_7_out), .sel(comparator_5_eq));
  Multiplexer #(.width(8)) multiplexer_8 (
    .in0(multiplexer_5_out), .in1(adder_3_out), .out(multiplexer_8_out), .sel(and_1_out));
  Multiplexer #(.width(2)) multiplexer_9 (.in0(and_6_out), .in1(2'b00), .out(multiplexer_9_out), .sel(reset));
  Multiplexer #(.width(2)) multiplexer_10 (.in0(core_reset_op), .in1(and_4_out), .out(multiplexer_10_out), .sel(start));
  Multiplexer #(.width(8)) multiplexer_11 (
    .in0(c_b_id_0_op), .in1(blocks_dispatched_q), .out(multiplexer_11_out), .sel(and_2_out));
  Multiplexer #(.width(8)) multiplexer_12 (
    .in0(c_b_id_1_op), .in1(multiplexer_5_out), .out(multiplexer_12_out), .sel(and_1_out));
  Multiplexer #(.width(3)) multiplexer_13 (
    .in0(c_t_cnt_0_op), .in1(multiplexer_6_out), .out(multiplexer_13_out), .sel(and_2_out));
  Multiplexer #(.width(3)) multiplexer_14 (
    .in0(c_t_cnt_1_op), .in1(multiplexer_7_out), .out(multiplexer_14_out), .sel(and_1_out));
  Multiplexer multiplexer_15 (.in0(done_op), .in1(1'b1), .out(multiplexer_15_out), .sel(and_3_out));
  Register #(.width(2)) core_start (.D(multiplexer_9_out), .en(1'b1), .clk(clock), .Q(core_start_op));  // open: clr
  Register #(.width(2)) core_reset (.D(multiplexer_16_out), .en(1'b1), .clk(clock), .Q(core_reset_op));  // open: clr
  Multiplexer #(.width(2)) multiplexer_16 (
    .in0(multiplexer_10_out), .in1(2'b11), .out(multiplexer_16_out), .sel(reset));
  Register core_block_id_0 (.D(multiplexer_17_out), .en(1'b1), .clk(clock), .Q(c_b_id_0_op));  // open: clr
  Multiplexer #(.width(8)) multiplexer_17 (
    .in0(multiplexer_11_out), .in1({8{1'b0}}), .out(multiplexer_17_out), .sel(reset));
  Register core_block_id_1 (.D(multiplexer_18_out), .en(1'b1), .clk(clock), .Q(c_b_id_1_op));  // open: clr
  Multiplexer #(.width(8)) multiplexer_18 (
    .in0(multiplexer_12_out), .in1({8{1'b0}}), .out(multiplexer_18_out), .sel(reset));
  Register #(.width(3)) core_thread_count_0 (
    .D(multiplexer_19_out), .en(1'b1), .clk(clock), .Q(c_t_cnt_0_op));  // open: clr
  Multiplexer #(.width(3)) multiplexer_19 (
    .in0(multiplexer_13_out), .in1(3'b100), .out(multiplexer_19_out), .sel(reset));
  Register #(.width(3)) core_thread_count_1 (
    .D(multiplexer_20_out), .en(1'b1), .clk(clock), .Q(c_t_cnt_1_op));  // open: clr
  Multiplexer #(.width(3)) multiplexer_20 (
    .in0(multiplexer_14_out), .in1(3'b100), .out(multiplexer_20_out), .sel(reset));
  Register #(.width(1)) done (.D(multiplexer_21_out), .en(1'b1), .clk(clock), .Q(done_op));  // open: clr
  Multiplexer multiplexer_21 (.in0(multiplexer_15_out), .in1(1'b0), .out(multiplexer_21_out), .sel(reset));
  or or_1 (or_1_out, core_start_op[0], and_2_out);
  or or_2 (or_2_out, and_1_out, core_start_op[1]);
  and and_4 (and_4_out[0], core_done[0], core_start_op[0]);
  and and_5 (and_4_out[1], core_done[1], core_start_op[1]);
  not not_2 (not_2_out, and_4_out[0]);
  and and_6 (and_6_out[0], not_2_out, or_1_out);
  not not_3 (not_3_out, and_4_out[1]);
  and and_7 (and_6_out[1], not_3_out, or_2_out);
  assign bit_extender_4_out = {{1{1'b0}}, and_4_out[0]};  // Bit_Extender bit_extender_4
  assign bit_extender_5_out = {{1{1'b0}}, and_4_out[1]};  // Bit_Extender bit_extender_5
  Adder #(.width(2)) adder_4 (.a(bit_extender_4_out), .b(bit_extender_5_out), .out(adder_4_out));  // open: cin, cout
  assign bit_extender_6_out = {{6{1'b0}}, adder_4_out};  // Bit_Extender bit_extender_6
  Adder adder_5 (.a(bit_extender_6_out), .b(blocks_done_q), .out(adder_5_out));  // open: cin, cout
endmodule

module GPU (
  input  start,
  input  clock,
  input  reset
);

  wire [1:0] core_1_done_op, dispatcher_1_core_reset_op, dispatcher_1_core_start_op;
  wire [2:0] dispatcher_1_c_t_cnt_0_op, dispatcher_1_c_t_cnt_1_op;
  wire [7:0] bit_extender_1_out, bit_extender_2_out, dcr_1_thread_count, dispatcher_1_c_b_id_0_op,
       dispatcher_1_c_b_id_1_op;

  Dispatcher dispatcher_1 (
    .core_done(core_1_done_op), .thread_count(dcr_1_thread_count), .start(start), .clock(clock),
    .reset(reset), .core_start_op(dispatcher_1_core_start_op), .core_reset_op(dispatcher_1_core_reset_op),
    .c_b_id_0_op(dispatcher_1_c_b_id_0_op), .c_b_id_1_op(dispatcher_1_c_b_id_1_op),
    .c_t_cnt_0_op(dispatcher_1_c_t_cnt_0_op), .c_t_cnt_1_op(dispatcher_1_c_t_cnt_1_op));  // open: done_op
  assign bit_extender_1_out = {{5{1'b0}}, dispatcher_1_c_t_cnt_0_op};  // Bit_Extender bit_extender_1
  DCR dcr_1 (.clock(clock), .reset(reset), .thread_count(dcr_1_thread_count));  // open: d_ctl_data, d_ctl_wr_enable
  Core core_1 (
    .start(dispatcher_1_core_start_op[0]), .clock(clock), .reset(dispatcher_1_core_reset_op[0]),
    .blk_id_in(dispatcher_1_c_b_id_0_op), .thread_count(bit_extender_1_out), .done_op(core_1_done_op[0]));  // open: p_m_rd_ready, p_m_rd_data, d2_m_rd_data, d3_m_rd_data, d1_m_rd_data, d0_m_rd_data, d0_m_rd_ready, d1_m_rd_ready, d2_m_rd_ready, d3_m_rd_ready, d0_m_wr_ready, d1_m_wr_ready, d2_m_wr_ready, d3_m_wr_ready, p_m_rd_valid, p_m_rd_addr, d3_m_wr_valid, d1_m_wr_valid, d2_m_wr_valid, d0_m_wr_valid, d3_m_wr_addr, d1_m_wr_addr, d2_m_wr_addr, d0_m_wr_addr, d3_m_wr_data, d0_m_wr_data, d1_m_wr_data, d2_m_wr_data, d3_m_rd_valid, d0_m_rd_valid, d2_m_rd_valid, d1_m_rd_valid, d3_m_rd_addr, d0_m_rd_addr, d2_m_rd_addr, d1_m_rd_addr
  assign bit_extender_2_out = {{5{1'b0}}, dispatcher_1_c_t_cnt_1_op};  // Bit_Extender bit_extender_2
  Core core_2 (
    .start(dispatcher_1_core_start_op[1]), .clock(clock), .reset(dispatcher_1_core_reset_op[1]),
    .blk_id_in(dispatcher_1_c_b_id_1_op), .thread_count(bit_extender_2_out), .done_op(core_1_done_op[1]));  // open: p_m_rd_ready, p_m_rd_data, d2_m_rd_data, d3_m_rd_data, d1_m_rd_data, d0_m_rd_data, d0_m_rd_ready, d1_m_rd_ready, d2_m_rd_ready, d3_m_rd_ready, d0_m_wr_ready, d1_m_wr_ready, d2_m_wr_ready, d3_m_wr_ready, p_m_rd_valid, p_m_rd_addr, d3_m_wr_valid, d1_m_wr_valid, d2_m_wr_valid, d0_m_wr_valid, d3_m_wr_addr, d1_m_wr_addr, d2_m_wr_addr, d0_m_wr_addr, d3_m_wr_data, d0_m_wr_data, d1_m_wr_data, d2_m_wr_data, d3_m_rd_valid, d0_m_rd_valid, d2_m_rd_valid, d1_m_rd_valid, d3_m_rd_addr, d0_m_rd_addr, d2_m_rd_addr, d1_m_rd_addr
endmodule

module ProgramMemController (
  input  [15:0] m_rd_data,
  input  m_rd_rdy,
  input  c0_rd_val,
  input  c1_rd_val,
  input  clock,
  input  reset,
  input  [7:0] c0_rd_adr,
  input  [7:0] c1_rd_adr,
  output [15:0] c0_rd_dat,
  output [15:0] c1_rd_dat,
  output [2:0] c_st_op,
  output m_rd_val,
  output c0_rd_rdy,
  output [7:0] m_rd_adr,
  output c1_rd_rdy
);

  wire and_1_out, and_2_out, and_3_out, and_4_out, and_5_out, and_6_out, and_7_out, comparator_1_eq,
       comparator_2_eq, comparator_3_eq, curr_consumer_q, multiplexer_2_out, multiplexer_4_out,
       multiplexer_6_out, multiplexer_9_out, multiplexer_12_out, multiplexer_13_out, multiplexer_17_out,
       multiplexer_18_out, multiplexer_19_out, multiplexer_20_out, multiplexer_23_out, multiplexer_24_out,
       not_1_out, not_2_out, not_3_out, not_4_out, not_5_out, not_6_out, or_1_out;
  wire [2:0] multiplexer_1_out, multiplexer_3_out, multiplexer_5_out, multiplexer_8_out, multiplexer_11_out,
       multiplexer_15_out, multiplexer_16_out;
  wire [7:0] multiplexer_7_out, multiplexer_10_out, multiplexer_14_out;
  wire [15:0] multiplexer_21_out, multiplexer_22_out, multiplexer_25_out, multiplexer_26_out;

  not not_1 (not_1_out, c0_rd_val);
  Comparator #(.mode("unsigned"), .width(3)) comparator_1 (
    .a(3'b000), .b(c_st_op), .eq(comparator_1_eq));  // open: gt, lt
  Multiplexer #(.width(3)) multiplexer_1 (.in0(c_st_op), .in1(3'b010), .out(multiplexer_1_out), .sel(or_1_out));
  and and_1 (and_1_out, not_1_out, c1_rd_val);
  Multiplexer multiplexer_2 (.in0(curr_consumer_q), .in1(and_1_out), .out(multiplexer_2_out), .sel(and_3_out));
  Comparator #(.mode("unsigned"), .width(3)) comparator_2 (
    .a(3'b100), .b(c_st_op), .eq(comparator_2_eq));  // open: gt, lt
  Comparator #(.mode("unsigned"), .width(3)) comparator_3 (
    .a(3'b010), .b(c_st_op), .eq(comparator_3_eq));  // open: gt, lt
  Multiplexer #(.width(3)) multiplexer_3 (.in0(c_st_op), .in1(3'b100), .out(multiplexer_3_out), .sel(m_rd_rdy));
  and and_2 (and_2_out, comparator_3_eq, m_rd_rdy);
  or or_1 (or_1_out, and_1_out, c0_rd_val);
  Multiplexer multiplexer_4 (.in0(multiplexer_2_out), .in1(1'b0), .out(multiplexer_4_out), .sel(reset));
  Multiplexer #(.width(3)) multiplexer_5 (.in0(c_st_op), .in1(3'b000), .out(multiplexer_5_out), .sel(not_2_out));
  Multiplexer multiplexer_6 (.in0(c0_rd_val), .in1(c1_rd_val), .out(multiplexer_6_out), .sel(curr_consumer_q));
  Register #(.width(1)) curr_consumer (
    .D(multiplexer_4_out), .en(1'b1), .clk(clock), .Q(curr_consumer_q));  // open: clr
  Multiplexer #(.width(8)) multiplexer_7 (.in0(c0_rd_adr), .in1(c1_rd_adr), .out(multiplexer_7_out), .sel(and_1_out));
  Multiplexer #(.width(3)) multiplexer_8 (
    .in0(c_st_op), .in1(multiplexer_1_out), .out(multiplexer_8_out), .sel(comparator_1_eq));
  not not_2 (not_2_out, multiplexer_6_out);
  Multiplexer multiplexer_9 (.in0(m_rd_val), .in1(1'b1), .out(multiplexer_9_out), .sel(and_3_out));
  Multiplexer #(.width(8)) multiplexer_10 (
    .in0(m_rd_adr), .in1(multiplexer_7_out), .out(multiplexer_10_out), .sel(and_3_out));
  Multiplexer #(.width(3)) multiplexer_11 (
    .in0(multiplexer_8_out), .in1(multiplexer_3_out), .out(multiplexer_11_out), .sel(comparator_3_eq));
  and and_3 (and_3_out, comparator_1_eq, or_1_out);
  Multiplexer multiplexer_12 (.in0(multiplexer_9_out), .in1(1'b0), .out(multiplexer_12_out), .sel(and_2_out));
  Multiplexer multiplexer_13 (.in0(multiplexer_12_out), .in1(1'b0), .out(multiplexer_13_out), .sel(reset));
  Multiplexer #(.width(8)) multiplexer_14 (
    .in0(multiplexer_10_out), .in1({8{1'b0}}), .out(multiplexer_14_out), .sel(reset));
  Multiplexer #(.width(3)) multiplexer_15 (
    .in0(multiplexer_11_out), .in1(multiplexer_5_out), .out(multiplexer_15_out), .sel(comparator_2_eq));
  Register #(.width(1)) m_rd_val_reg (.D(multiplexer_13_out), .en(1'b1), .clk(clock), .Q(m_rd_val));  // open: clr
  Register m_rd_addr_reg (.D(multiplexer_14_out), .en(1'b1), .clk(clock), .Q(m_rd_adr));  // open: clr
  not not_3 (not_3_out, curr_consumer_q);
  not not_4 (not_4_out, c0_rd_val);
  not not_5 (not_5_out, curr_consumer_q);
  not not_6 (not_6_out, c1_rd_val);
  Multiplexer #(.width(3)) multiplexer_16 (
    .in0(multiplexer_15_out), .in1(3'b000), .out(multiplexer_16_out), .sel(reset));
  Register #(.width(3)) controller_state (.D(multiplexer_16_out), .en(1'b1), .clk(clock), .Q(c_st_op));  // open: clr
  and and_4 (and_4_out, comparator_3_eq, m_rd_rdy, not_3_out);
  and and_5 (and_5_out, comparator_3_eq, m_rd_rdy, curr_consumer_q);
  and and_6 (and_6_out, comparator_2_eq, not_4_out, not_5_out);
  and and_7 (and_7_out, comparator_2_eq, not_6_out, curr_consumer_q);
  Multiplexer multiplexer_17 (.in0(c0_rd_rdy), .in1(1'b1), .out(multiplexer_17_out), .sel(and_4_out));
  Multiplexer multiplexer_18 (.in0(multiplexer_17_out), .in1(1'b0), .out(multiplexer_18_out), .sel(and_6_out));
  Multiplexer multiplexer_19 (.in0(c1_rd_rdy), .in1(1'b1), .out(multiplexer_19_out), .sel(and_5_out));
  Multiplexer multiplexer_20 (.in0(multiplexer_19_out), .in1(1'b0), .out(multiplexer_20_out), .sel(and_7_out));
  Multiplexer #(.width(16)) multiplexer_21 (
    .in0(c0_rd_dat), .in1(m_rd_data), .out(multiplexer_21_out), .sel(and_4_out));
  Multiplexer #(.width(16)) multiplexer_22 (
    .in0(c1_rd_dat), .in1(m_rd_data), .out(multiplexer_22_out), .sel(and_5_out));
  Register #(.width(1)) c0_rd_rdy_reg (.D(multiplexer_23_out), .en(1'b1), .clk(clock), .Q(c0_rd_rdy));  // open: clr
  Multiplexer multiplexer_23 (.in0(multiplexer_18_out), .in1(1'b0), .out(multiplexer_23_out), .sel(reset));
  Register #(.width(1)) register_1 (.D(multiplexer_24_out), .en(1'b1), .clk(clock), .Q(c1_rd_rdy));  // open: clr
  Multiplexer multiplexer_24 (.in0(multiplexer_20_out), .in1(1'b0), .out(multiplexer_24_out), .sel(reset));
  Multiplexer #(.width(16)) multiplexer_25 (
    .in0(multiplexer_21_out), .in1({16{1'b0}}), .out(multiplexer_25_out), .sel(reset));
  Multiplexer #(.width(16)) multiplexer_26 (
    .in0(multiplexer_22_out), .in1({16{1'b0}}), .out(multiplexer_26_out), .sel(reset));
  Register #(.width(16)) c0_rd_data_reg (.D(multiplexer_25_out), .en(1'b1), .clk(clock), .Q(c0_rd_dat));  // open: clr
  Register #(.width(16)) register_2 (.D(multiplexer_26_out), .clk(clock), .Q(c1_rd_dat));  // open: en, clr
endmodule
